// Logisim project Project2.circ as structural Verilog: 4 circuits, main circuit main
module main (
  input  Program_check,
  input  Indirect,
  input  C1,
  input  Clock,
  input  Reset,
  output Fetch,
  output Decode,
  output Indirect_2,
  output Execute,
  output Trap,
  output S1,
  output S2
);

  wire and_1_out, and_2_out, not_1_out, not_2_out, not_3_out, not_4_out, not_5_out, or_1_out, or_2_out,
       or_3_out, State0_qn, State1_qn, State2_qn;

  not not_1 (not_1_out, State0_qn);
  not not_2 (not_2_out, State1_qn);
  not not_3 (not_3_out, State0_qn);
  not not_4 (not_4_out, State2_qn);
  and and_1 (and_1_out, not_1_out, State2_qn, not_2_out, Indirect);
  not not_5 (not_5_out, or_1_out);
  or or_1 (or_1_out, State0_qn, State1_qn, State2_qn, C1);
  and and_2 (and_2_out, not_3_out, Program_check, not_4_out, State1_qn);
  or or_2 (or_2_out, and_1_out, not_5_out);
  or or_3 (or_3_out, Reset, S1);
  SR_Master_Slave State0 (.Input(and_2_out), .Clk(Clock), .Qn(State0_qn));  // open: Q
  SR_Master_Slave State1 (.Input(State2_qn), .Clk(Clock), .Qn(State1_qn));  // open: Q
  SR_Master_Slave State2 (.Input(or_2_out), .Clk(Clock), .Qn(State2_qn));  // open: Q
  SR_Master_Slave S (.Input(or_3_out), .Clk(Clock), .Qn(S2), .Q(S1));
  _3_8_Decoder u_3_8_decoder_1 (
    .Input2(State0_qn), .Input1(State1_qn), .Input0(State2_qn), .Output0(Fetch), .Output1(Decode),
    .Output2(Execute), .Output3(Indirect_2), .Output4(Trap));  // open: Output5, Output6, Output7
endmodule

// D
module SR_Master_Slave (
  input  Input,
  input  Clk,
  output Qn,
  output Q
);

  wire and_1_out, and_2_out, and_3_out, and_4_out, and_5_out, and_6_out, and_7_out, and_8_out, not_1_out,
       not_2_out, not_3_out, not_4_out, not_5_out, not_6_out, not_7_out, not_8_out;

  not not_1 (not_1_out, Input);
  not not_2 (not_2_out, and_1_out);
  and and_1 (and_1_out, Input, Clk);
  and and_2 (and_2_out, Clk, not_1_out);
  not not_3 (not_3_out, and_2_out);
  and and_3 (and_3_out, not_2_out, not_6_out);
  and and_4 (and_4_out, not_5_out, not_3_out);
  not not_4 (not_4_out, Clk);
  not not_5 (not_5_out, and_3_out);
  not not_6 (not_6_out, and_4_out);
  and and_5 (and_5_out, not_5_out, not_4_out);
  and and_6 (and_6_out, not_4_out, not_6_out);
  not not_7 (not_7_out, and_5_out);
  not not_8 (not_8_out, and_6_out);
  and and_7 (and_7_out, not_7_out, Q);
  not not_9 (Qn, and_7_out);
  not not_10 (Q, and_8_out);
  and and_8 (and_8_out, Qn, not_8_out);
endmodule

// 3-8
module _3_8_Decoder (
  input  Input2,
  input  Input1,
  input  Input0,
  output Output0,
  output Output1,
  output Output2,
  output Output3,
  output Output4,
  output Output5,
  output Output6,
  output Output7
);

  wire not_1_out, not_2_out, not_3_out;

  not not_1 (not_1_out, Input2);
  not not_2 (not_2_out, Input1);
  not not_3 (not_3_out, Input0);
  and and_1 (Output0, not_1_out, not_2_out, not_3_out);
  and and_2 (Output1, not_1_out, not_2_out, Input0);
  and and_3 (Output2, not_1_out, Input1, not_3_out);
  and and_4 (Output3, not_1_out, Input1, Input0);
  and and_5 (Output4, Input2, not_2_out, not_3_out);
  and and_6 (Output5, Input2, not_2_out, Input0);
  and and_7 (Output6, Input2, Input1, not_3_out);
  and and_8 (Output7, Input2, Input1, Input0);
endmodule

// S
module S_enable (
  input  S,
  input  Previous,
  input  New,
  output Output
);

  wire and_1_out, and_2_out, not_1_out;

  not not_1 (not_1_out, S);
  and and_1 (and_1_out, not_1_out, Previous);
  and and_2 (and_2_out, S, New);
  or or_1 (Output, and_1_out, and_2_out);
endmodule
