// Logisim project Project3u.circ as structural Verilog: 26 circuits, main circuit IROutputs
// Decode
module IROutputs (
  input  [15:0] Instruction_Register,
  output [3:0] Opcode,
  output [11:0] Long_Offset,
  output S,
  output [1:0] Shift,
  output [2:0] Rs1,
  output [2:0] Rs2,
  output [7:0] Short_Offset,
  output [2:0] Rd
);

  wire nor_1_out, nor_2_out, or_1_out;

  nor nor_1 (nor_1_out, Instruction_Register[0], Instruction_Register[2]);
  Multiplexer #(.width(3), .enable("false")) multiplexer_1 (
    .in0(Instruction_Register[9:7]), .in1(Instruction_Register[7:5]), .out(Rd), .sel(or_1_out));
  nor nor_2 (nor_2_out, Instruction_Register[0], Instruction_Register[1]);
  or or_1 (or_1_out, nor_1_out, nor_2_out);

  assign Long_Offset = Instruction_Register[15:4];
  assign Opcode = Instruction_Register[3:0];
  assign Rs1 = Instruction_Register[12:10];
  assign Rs2 = Instruction_Register[15:13];
  assign S = Instruction_Register[4];
  assign Shift = Instruction_Register[6:5];
  assign Short_Offset = Instruction_Register[15:8];
endmodule

module MAR (
  input  [15:0] Input,
  input  Enable,
  input  Clock,
  input  Clear,
  output [15:0] Output
);

  Register #(.width(16)) MAR_Register (.D(Input), .en(Enable), .Q(Output), .clk(Clock), .clr(Clear));
endmodule

module MDR (
  input  [15:0] Output,
  input  Enable,
  input  Clock,
  input  Clear,
  output [15:0] Output_2
);

  Register #(.width(16)) MDR_Register (.D(Output), .en(Enable), .Q(Output_2), .clk(Clock), .clr(Clear));
endmodule

module IR (
  input  [15:0] Input,
  input  Enable,
  input  Clock,
  input  Clear,
  output [15:0] Output
);

  Register #(.width(16)) MDR_Register (.D(Input), .en(Enable), .Q(Output), .clk(Clock), .clr(Clear));
endmodule

module GPR (
  input  [15:0] Input,
  input  Clock,
  input  Clear,
  input  Enable,
  input  [2:0] Selection_Bits,
  output [15:0] Output
);

  wire decoder_1_out0, decoder_1_out1, decoder_1_out2, decoder_1_out3, decoder_1_out4, decoder_1_out5,
       decoder_1_out6, decoder_1_out7;
  wire [15:0] Reg0_q, Reg1_q, Reg2_q, Reg3_q, Reg4_q, Reg5_q, Reg6_q, Reg7_q;

  Decoder #(.select(3)) decoder_1 (
    .out0(decoder_1_out0), .out1(decoder_1_out1), .out2(decoder_1_out2), .out3(decoder_1_out3),
    .out4(decoder_1_out4), .out5(decoder_1_out5), .out6(decoder_1_out6), .out7(decoder_1_out7),
    .sel(Selection_Bits), .en(Enable));
  Register #(.width(16)) Reg0 (.D(Input), .en(decoder_1_out0), .Q(Reg0_q), .clk(Clock), .clr(Clear));
  Register #(.width(16)) Reg1 (.D(Input), .en(decoder_1_out1), .Q(Reg1_q), .clk(Clock), .clr(Clear));
  Register #(.width(16)) Reg2 (.D(Input), .en(decoder_1_out2), .Q(Reg2_q), .clk(Clock), .clr(Clear));
  Register #(.width(16)) Reg3 (.D(Input), .en(decoder_1_out3), .Q(Reg3_q), .clk(Clock), .clr(Clear));
  Register #(.width(16)) Reg4 (.D(Input), .en(decoder_1_out4), .Q(Reg4_q), .clk(Clock), .clr(Clear));
  Register #(.width(16)) Reg5 (.D(Input), .en(decoder_1_out5), .Q(Reg5_q), .clk(Clock), .clr(Clear));
  Register #(.width(16)) Reg6 (.D(Input), .en(decoder_1_out6), .Q(Reg6_q), .clk(Clock), .clr(Clear));
  Register #(.width(16)) Reg7 (.D(Input), .en(decoder_1_out7), .Q(Reg7_q), .clk(Clock), .clr(Clear));
  Multiplexer #(.select(3), .width(16), .enable("false")) multiplexer_1 (
    .in0(Reg0_q), .in1(Reg1_q), .in2(Reg2_q), .in3(Reg3_q), .in4(Reg4_q), .in5(Reg5_q), .in6(Reg6_q),
    .in7(Reg7_q), .out(Output), .sel(Selection_Bits));
endmodule

module PSW (
  input  [15:0] Output,
  input  Enable,
  input  Clock,
  input  Clear,
  output [15:0] Output_2
);

  Register #(.width(16)) PSW_Register (.D(Output), .en(Enable), .Q(Output_2), .clk(Clock), .clr(Clear));
endmodule

module main (
  input  in_1,
  input  Clk,
  input  Clear
);

  wire A1, B0_OUT, B1, C1, CC_N, CC_Z, Execute, Fetch, GPRin, GPRout, IRin, IRShiftout, IRShortout, MARin,
       MARout, MDRin, MDRout, PSW_P, PSWin, PSWout, Read_mm, Reset, S, Set_CC, Timeout, Trap, WMFC, Write_mm,
       Yin, Yout, Zin, Zout;
  wire [1:0] Shift;
  wire [2:0] GPRsel, Rd, Rs1, Rs2;
  wire [3:0] ALUSel, Opcode, State;
  wire [7:0] Short_Offset;
  wire [11:0] Long_Offset;
  wire [15:0] alu_1_out_5, controlled_buffer_1_out, gpr_1_output, ir_1_output, mar_1_output, mdr_1_output_2,
       ram_1_data, y_1_output, z_1_output;
  wire [15:3] psw_1_output_2;

  assign controlled_buffer_1_out = MARout ? mar_1_output : 16'bz;  // Controlled_Buffer controlled_buffer_1
  assign controlled_buffer_1_out = MDRout ? mdr_1_output_2 : 16'bz;  // Controlled_Buffer controlled_buffer_2
  assign controlled_buffer_1_out = IRShiftout ? {{14{1'b0}}, Shift} : 16'bz;  // Controlled_Buffer controlled_buffer_3
  assign controlled_buffer_1_out = IRShortout ? {{8{1'b0}}, Short_Offset} : 16'bz;  // Controlled_Buffer controlled_buffer_4
  assign controlled_buffer_1_out = PSWout ? {psw_1_output_2, PSW_P, CC_N, CC_Z} : 16'bz;  // Controlled_Buffer controlled_buffer_5
  assign controlled_buffer_1_out = GPRout ? gpr_1_output : 16'bz;  // Controlled_Buffer controlled_buffer_6
  assign controlled_buffer_1_out = Yout ? y_1_output : 16'bz;  // Controlled_Buffer controlled_buffer_7
  assign controlled_buffer_1_out = Zout ? z_1_output : 16'bz;  // Controlled_Buffer controlled_buffer_8
  MAR mar_1 (.Input(controlled_buffer_1_out), .Enable(MARin), .Clock(Clk), .Clear(Clear), .Output(mar_1_output));
  MDR mdr_1 (.Output(ram_1_data), .Enable(MDRin), .Clock(Clk), .Clear(Clear), .Output_2(mdr_1_output_2));
  IR ir_1 (.Input(controlled_buffer_1_out), .Enable(IRin), .Clock(Clk), .Clear(Clear), .Output(ir_1_output));
  PSW psw_1 (
    .Output(controlled_buffer_1_out), .Enable(PSWin), .Clock(Clk), .Clear(Clear),
    .Output_2({psw_1_output_2, PSW_P, CC_N, CC_Z}));
  GPR gpr_1 (
    .Input(controlled_buffer_1_out), .Clock(GPRin), .Clear(Clk), .Enable(Clear), .Selection_Bits(GPRsel),
    .Output(gpr_1_output));
  y y_1 (.Input(controlled_buffer_1_out), .Enable(Yin), .Clock(Clk), .Clear(Clear), .Output(y_1_output));
  ALU alu_1 (
    .Left(controlled_buffer_1_out), .Right(y_1_output), .Selector_Bits(ALUSel), .out_5(alu_1_out_5));  // open: Enable
  z z_1 (.Input(alu_1_out_5), .Enable(Zin), .Clock(Clk), .Clear(Clear), .Output(z_1_output));
  IROutputs iroutputs_1 (
    .Instruction_Register(ir_1_output), .Opcode(Opcode), .Long_Offset(Long_Offset), .S(S), .Shift(Shift),
    .Rs1(Rs1), .Rs2(Rs2), .Short_Offset(Short_Offset), .Rd(Rd));
  RAM #(.addrWidth(16), .dataWidth(16), .bus("separate")) ram_1 (
    .addr(mar_1_output), .din(mdr_1_output_2), .data(ram_1_data), .str(Write_mm), .sel(in_1), .clk(Clk),
    .ld(Read_mm), .clr(Clear));
  Step_State step_state_1 (
    .Timeout(Timeout), .CC_N(CC_N), .CC_Z(CC_Z), .PSW_P(PSW_P), .Clear(Clear), .Opcode_In(Opcode),
    .Clock_In(Reset), .State(State), .Fetch(Fetch), .Execute(Execute), .Trap(Trap), .B0_Out(B0_OUT));
  Signals signals_1 (
    .State(State), .Step({C1, B1, A1}), .Opcode(Opcode), .IR_Rd(Rd), .IR_RS1(Rs1), .IR_RS2(Rs2),
    .Read_mm(Read_mm), .Write_mm(Write_mm), .WMFC(WMFC), .SET_CC(Set_CC), .Z_OUT(Zout), .Z_IN(Zin),
    .Y_IN(Yin), .PSW_OUT(PSWout), .MDR_OUT(MDRout), .MDR_IN(MDRin), .MAR_OUT(MARout), .MAR_IN(MARin),
    .IR_IN(IRin), .IR_SHORT_OUT(IRShortout), .IR_SHIFT_OUT(IRShiftout), .GPR_OUT(GPRout), .GPR_IN(GPRin),
    .GPR_SEL(GPRsel), .ALU_SEL(ALUSel));
  Counter counter_1 (.Reset(Reset), .Clk(Clk), .A1(A1), .B1(B1), .C1(C1));

  // Other names for the same wires on the sheet: Step[2:0] = {C1, B1, A1}
endmodule

// Y
module y (
  input  [15:0] Input,
  input  Enable,
  input  Clock,
  input  Clear,
  output [15:0] Output
);

  Register #(.width(16)) Y_Register (.D(Input), .en(Enable), .Q(Output), .clk(Clock), .clr(Clear));
endmodule

// Z
module z (
  input  [15:0] Input,
  input  Enable,
  input  Clock,
  input  Clear,
  output [15:0] Output
);

  Register #(.width(16)) Z_Register (.D(Input), .en(Enable), .Q(Output), .clk(Clock), .clr(Clear));
endmodule

// Cycle
module Counter (
  input  Reset,
  input  Clk,
  output A1,
  output B1,
  output C1
);

  wire and_1_out, and_2_out, d_ff_1_qn, or_1_out, xor_1_out;

  and and_1 (and_1_out, C1, B1);
  or or_1 (or_1_out, and_1_out, A1);
  xor xor_1 (xor_1_out, B1, C1);
  D_Flip_Flop A (.clk(Clk), .D(or_1_out), .Q(A1), .en(1'b1), .reset(and_2_out));  // open: Qn, preset
  D_Flip_Flop B (.clk(Clk), .D(xor_1_out), .Q(B1), .en(1'b1), .reset(and_2_out));  // open: Qn, preset
  D_Flip_Flop d_ff_1 (.clk(Clk), .D(d_ff_1_qn), .Q(C1), .Qn(d_ff_1_qn), .en(1'b1), .reset(and_2_out));  // open: preset
  and and_2 (and_2_out, Clk, Reset);
endmodule

module XOR (
  input  A,
  input  B,
  output Output
);

  wire and_1_out, not_1_out, or_1_out;

  and and_1 (and_1_out, A, B);
  or or_1 (or_1_out, B, A);
  not not_1 (not_1_out, and_1_out);
  and and_2 (Output, not_1_out, or_1_out);
endmodule

module Adder_1_Bit (
  input  IN_Left,
  input  IN_Right,
  input  C_IN,
  output OUT,
  output C_OUT
);

  wire and_1_out, and_2_out, not_1_out, or_1_out, xor_1_output;

  XOR xor_1 (.A(IN_Left), .B(IN_Right), .Output(xor_1_output));
  and and_1 (and_1_out, IN_Right, not_1_out, IN_Left);
  not not_1 (not_1_out, C_IN);
  or or_1 (or_1_out, IN_Left, IN_Right);
  and and_2 (and_2_out, or_1_out, C_IN);
  or or_2 (C_OUT, and_1_out, and_2_out);
  XOR xor_2 (.A(xor_1_output), .B(C_IN), .Output(OUT));
endmodule

module Adder (
  input  [15:0] in_1,
  input  [15:0] in_2,
  output [15:0] out_3
);

  wire adder_1_bit_1_p3, adder_1_bit_2_p3, adder_1_bit_3_p3, adder_1_bit_4_p3, adder_1_bit_5_p3,
       adder_1_bit_6_p3, adder_1_bit_7_p3, adder_1_bit_8_p3, adder_1_bit_9_p3, adder_1_bit_10_p3,
       adder_1_bit_11_p3, adder_1_bit_12_p3, adder_1_bit_13_p3, adder_1_bit_14_p3, adder_1_bit_15_p3;

  // Adder_1_Bit adder_1_bit_1: pin names not known; wires that end beside it: in_1[15], in_2[15], adder_1_bit_1_p3, out_3[15]
  // Adder_1_Bit adder_1_bit_2: pin names not known; wires that end beside it: in_1[14], in_2[14], adder_1_bit_2_p3, out_3[15], adder_1_bit_1_p3, out_3[14]
  // Adder_1_Bit adder_1_bit_3: pin names not known; wires that end beside it: in_1[13], in_2[13], adder_1_bit_3_p3, out_3[14], adder_1_bit_2_p3, out_3[13]
  // Adder_1_Bit adder_1_bit_4: pin names not known; wires that end beside it: in_1[12], in_2[12], adder_1_bit_4_p3, out_3[13], adder_1_bit_3_p3, out_3[12]
  // Adder_1_Bit adder_1_bit_5: pin names not known; wires that end beside it: in_1[11], in_2[11], adder_1_bit_5_p3, out_3[12], adder_1_bit_4_p3, out_3[11]
  // Adder_1_Bit adder_1_bit_6: pin names not known; wires that end beside it: in_1[10], in_2[10], adder_1_bit_6_p3, out_3[11], adder_1_bit_5_p3, out_3[10]
  // Adder_1_Bit adder_1_bit_7: pin names not known; wires that end beside it: in_1[9], in_2[9], adder_1_bit_7_p3, out_3[10], adder_1_bit_6_p3, out_3[9]
  // Adder_1_Bit adder_1_bit_8: pin names not known; wires that end beside it: in_1[8], in_2[8], adder_1_bit_8_p3, out_3[9], adder_1_bit_7_p3, out_3[8]
  // Adder_1_Bit adder_1_bit_9: pin names not known; wires that end beside it: in_1[7], in_2[7], adder_1_bit_9_p3, out_3[8], adder_1_bit_8_p3, out_3[7]
  // Adder_1_Bit adder_1_bit_10: pin names not known; wires that end beside it: in_1[6], in_2[6], adder_1_bit_10_p3, out_3[7], adder_1_bit_9_p3, out_3[6]
  // Adder_1_Bit adder_1_bit_11: pin names not known; wires that end beside it: in_1[5], in_2[5], adder_1_bit_11_p3, out_3[6], adder_1_bit_10_p3, out_3[5]
  // Adder_1_Bit adder_1_bit_12: pin names not known; wires that end beside it: in_1[4], in_2[4], adder_1_bit_12_p3, out_3[5], adder_1_bit_11_p3, out_3[4]
  // Adder_1_Bit adder_1_bit_13: pin names not known; wires that end beside it: in_1[3], in_2[3], adder_1_bit_13_p3, out_3[4], adder_1_bit_12_p3, out_3[3]
  // Adder_1_Bit adder_1_bit_14: pin names not known; wires that end beside it: in_1[2], in_2[2], adder_1_bit_14_p3, out_3[3], adder_1_bit_13_p3, out_3[2]
  // Adder_1_Bit adder_1_bit_15: pin names not known; wires that end beside it: in_1[1], in_2[1], adder_1_bit_15_p3, out_3[2], adder_1_bit_14_p3, out_3[1]
  // Adder_1_Bit adder_1_bit_16: pin names not known; wires that end beside it: in_1[0], in_2[0], 1'b0, out_3[1], adder_1_bit_15_p3, out_3[0]

  // Notes on the sheet:
  //   Highest Bit
  //   Lowest Bit
endmodule

module ZD (
  input  A,
  input  C,
  input  Opcode_6,
  input  Opcode_7,
  input  Opcode_12,
  output ZD
);

  or or_1 (ZD, A, C, Opcode_6, Opcode_7, Opcode_12);
endmodule

module ZC (
  input  C,
  input  D,
  input  E,
  input  Timeout,
  input  Opcode_6,
  input  Opcode_7,
  input  Opcode_8,
  input  Opcode_13,
  output ZB
);

  wire and_1_out;

  and and_1 (and_1_out, E, Timeout);
  or or_1 (ZB, C, D, Opcode_6, and_1_out, Opcode_7, Opcode_8, Opcode_13);
endmodule

module ZB (
  input  A,
  input  D,
  input  E,
  input  Timeout,
  input  Opcode_6,
  input  Opcode_7,
  input  Opcode_8,
  output ZB
);

  wire and_1_out, not_1_out, or_1_out;

  not not_1 (not_1_out, Timeout);
  and and_1 (and_1_out, E, not_1_out);
  or or_1 (or_1_out, A, D, and_1_out, Opcode_6, Opcode_7, Opcode_8);
  not not_2 (ZB, or_1_out);
endmodule

// States
module Step_State (
  input  Timeout,
  input  CC_N,
  input  CC_Z,
  input  PSW_P,
  input  Clear,
  input  [3:0] Opcode_In,
  input  Clock_In,
  output [3:0] State,
  output Fetch,
  output Execute,
  output Trap,
  output B0_Out
);

  wire and_1_out, and_2_out, and_3_out, and_4_out, and_5_out, and_6_out, and_7_out, and_8_out, and_9_out,
       and_10_out, and_11_out, and_12_out, and_13_out, and_14_out, and_15_out, Data_A0_qn, Data_B0_qn,
       Data_C0_qn, Data_D0_qn, decoder_1_out6, decoder_1_out7, decoder_1_out8, decoder_1_out9,
       decoder_1_out10, decoder_1_out11, decoder_1_out12, decoder_1_out13, decoder_1_out14, decoder_1_out15,
       not_1_out, not_2_out, not_3_out, not_4_out, not_5_out, not_6_out, or_1_out, or_2_out, or_3_out,
       or_4_out, or_5_out, or_6_out, or_7_out, zb_1_zb, zc_1_zb, zd_1_zd;

  Decoder #(.select(4)) decoder_1 (
    .out6(decoder_1_out6), .out7(decoder_1_out7), .out8(decoder_1_out8), .out9(decoder_1_out9),
    .out10(decoder_1_out10), .out11(decoder_1_out11), .out12(decoder_1_out12), .out13(decoder_1_out13),
    .out14(decoder_1_out14), .out15(decoder_1_out15), .sel(Opcode_In), .en(1'b1));  // open: out0, out1, out2, out3, out4, out5
  and and_1 (and_1_out, decoder_1_out9, CC_N);
  or or_1 (or_1_out, and_1_out, and_2_out, decoder_1_out11);
  and and_2 (and_2_out, decoder_1_out10, CC_Z);
  and and_3 (and_3_out, or_2_out, PSW_P);
  or or_2 (or_2_out, decoder_1_out14, decoder_1_out15);
  and and_4 (and_4_out, or_2_out, not_1_out);
  and and_5 (and_5_out, decoder_1_out9, not_3_out);
  not not_1 (not_1_out, PSW_P);
  or or_3 (or_3_out, and_5_out, and_6_out);
  and and_6 (and_6_out, decoder_1_out10, not_2_out);
  not not_2 (not_2_out, CC_Z);
  not not_3 (not_3_out, CC_N);
  ZB zb_1 (
    .A(or_1_out), .D(and_4_out), .E(or_3_out), .Timeout(Timeout), .Opcode_6(decoder_1_out6),
    .Opcode_7(decoder_1_out7), .Opcode_8(decoder_1_out8), .ZB(zb_1_zb));
  ZC zc_1 (
    .C(and_3_out), .D(and_4_out), .E(or_3_out), .Timeout(Timeout), .Opcode_6(decoder_1_out6),
    .Opcode_7(decoder_1_out7), .Opcode_8(decoder_1_out8), .Opcode_13(decoder_1_out13), .ZB(zc_1_zb));
  ZD zd_1 (
    .A(or_1_out), .C(and_3_out), .Opcode_6(decoder_1_out6), .Opcode_7(decoder_1_out7),
    .Opcode_12(decoder_1_out12), .ZD(zd_1_zd));
  not not_4 (not_4_out, or_3_out);
  not not_5 (not_5_out, and_4_out);
  and and_7 (and_7_out, Data_A0_qn, Data_C0_qn, zb_1_zb);
  and and_8 (and_8_out, Data_A0_qn, B0_Out, State[2], Data_D0_qn);
  and and_9 (and_9_out, Execute, not_6_out, Timeout);
  not not_6 (not_6_out, and_10_out);
  and and_10 (and_10_out, Execute, Data_B0_qn, decoder_1_out6, State[2], State[3]);
  and and_11 (and_11_out, Data_A0_qn, Data_C0_qn, zc_1_zb);
  and and_12 (and_12_out, Data_A0_qn, State[2], Data_D0_qn);
  and and_13 (and_13_out, zd_1_zd, Data_A0_qn, Data_C0_qn);
  and and_14 (and_14_out, Data_A0_qn, State[2], Data_D0_qn);
  and and_15 (and_15_out, not_4_out, Data_A0_qn, Data_C0_qn, not_5_out);
  or or_4 (or_4_out, and_10_out, and_15_out);
  or or_5 (or_5_out, and_7_out, and_8_out, and_9_out);
  or or_6 (or_6_out, and_9_out, and_11_out, and_12_out);
  or or_7 (or_7_out, and_13_out, and_14_out);
  D_Flip_Flop Data_A0 (
    .clk(Clock_In), .D(or_4_out), .Q(Execute), .Qn(Data_A0_qn), .preset(1'b0), .en(1'b1), .reset(Clear));
  D_Flip_Flop Data_B0 (
    .clk(Clock_In), .D(or_5_out), .Q(B0_Out), .Qn(Data_B0_qn), .preset(1'b0), .en(1'b1), .reset(Clear));
  D_Flip_Flop Data_C0 (
    .clk(Clock_In), .D(or_6_out), .Q(State[2]), .Qn(Data_C0_qn), .preset(1'b0), .en(1'b1), .reset(Clear));
  D_Flip_Flop Data_D0 (
    .clk(Clock_In), .D(or_7_out), .Q(State[3]), .Qn(Data_D0_qn), .preset(1'b0), .en(1'b1), .reset(Clear));
  and and_16 (Fetch, Data_A0_qn, Data_C0_qn);
  and and_17 (Trap, Data_A0_qn, State[2]);

  assign State[1:0] = {B0_Out, Execute};

  // Notes on the sheet:
  //   A
  //   B
  //   C
  //   D
  //   E
endmodule

module Add_Long_Offset (
  input  [15:0] In_Left,
  input  [15:0] In_Right,
  output [15:0] out_3
);

  _16_Bit_Adder u_16_bit_adder_1 (.in_1({{5{In_Left[11]}}, In_Left[10:0]}), .in_2(In_Right), .out_3(out_3));
endmodule

module Shift_Right (
  input  [15:0] Being_Shifted,
  input  [15:0] Shift_Amount,
  output [15:0] out_3
);

  wire multiplexer_1_out, multiplexer_2_out, multiplexer_3_out, multiplexer_4_out, multiplexer_5_out,
       multiplexer_6_out, multiplexer_7_out, multiplexer_8_out, multiplexer_9_out, multiplexer_10_out,
       multiplexer_11_out, multiplexer_12_out, multiplexer_13_out, multiplexer_14_out, multiplexer_15_out,
       multiplexer_16_out, multiplexer_17_out, multiplexer_18_out, multiplexer_19_out, multiplexer_20_out,
       multiplexer_21_out, multiplexer_22_out, multiplexer_23_out, multiplexer_24_out, multiplexer_25_out,
       multiplexer_26_out, multiplexer_27_out, multiplexer_28_out, multiplexer_29_out, multiplexer_30_out,
       multiplexer_31_out, multiplexer_32_out, multiplexer_33_out, multiplexer_34_out, multiplexer_35_out,
       multiplexer_36_out, multiplexer_37_out, multiplexer_38_out, multiplexer_39_out, multiplexer_40_out,
       multiplexer_41_out, multiplexer_42_out, multiplexer_43_out, multiplexer_44_out, multiplexer_45_out,
       multiplexer_46_out, multiplexer_47_out, multiplexer_48_out;

  Multiplexer multiplexer_1 (
    .in0(Being_Shifted[0]), .in1(Being_Shifted[1]), .out(multiplexer_1_out), .sel(Shift_Amount[0]));  // open: en
  Multiplexer multiplexer_2 (
    .in0(Being_Shifted[1]), .in1(Being_Shifted[2]), .out(multiplexer_2_out), .sel(Shift_Amount[0]));  // open: en
  Multiplexer multiplexer_3 (
    .in0(Being_Shifted[2]), .in1(Being_Shifted[3]), .out(multiplexer_3_out), .sel(Shift_Amount[0]));  // open: en
  Multiplexer multiplexer_4 (
    .in0(Being_Shifted[3]), .in1(Being_Shifted[4]), .out(multiplexer_4_out), .sel(Shift_Amount[0]));  // open: en
  Multiplexer multiplexer_5 (
    .in0(Being_Shifted[4]), .in1(Being_Shifted[5]), .out(multiplexer_5_out), .sel(Shift_Amount[0]));  // open: en
  Multiplexer multiplexer_6 (
    .in0(Being_Shifted[5]), .in1(Being_Shifted[6]), .out(multiplexer_6_out), .sel(Shift_Amount[0]));  // open: en
  Multiplexer multiplexer_7 (
    .in0(Being_Shifted[6]), .in1(Being_Shifted[7]), .out(multiplexer_7_out), .sel(Shift_Amount[0]));  // open: en
  Multiplexer multiplexer_8 (
    .in0(Being_Shifted[7]), .in1(Being_Shifted[8]), .out(multiplexer_8_out), .sel(Shift_Amount[0]));  // open: en
  Multiplexer multiplexer_9 (
    .in0(Being_Shifted[8]), .in1(Being_Shifted[9]), .out(multiplexer_9_out), .sel(Shift_Amount[0]));  // open: en
  Multiplexer multiplexer_10 (
    .in0(Being_Shifted[9]), .in1(Being_Shifted[10]), .out(multiplexer_10_out), .sel(Shift_Amount[0]));  // open: en
  Multiplexer multiplexer_11 (
    .in0(Being_Shifted[10]), .in1(Being_Shifted[11]), .out(multiplexer_11_out), .sel(Shift_Amount[0]));  // open: en
  Multiplexer multiplexer_12 (
    .in0(Being_Shifted[11]), .in1(Being_Shifted[12]), .out(multiplexer_12_out), .sel(Shift_Amount[0]));  // open: en
  Multiplexer multiplexer_13 (
    .in0(Being_Shifted[12]), .in1(Being_Shifted[13]), .out(multiplexer_13_out), .sel(Shift_Amount[0]));  // open: en
  Multiplexer multiplexer_14 (
    .in0(Being_Shifted[13]), .in1(Being_Shifted[14]), .out(multiplexer_14_out), .sel(Shift_Amount[0]));  // open: en
  Multiplexer multiplexer_15 (
    .in0(Being_Shifted[14]), .in1(Being_Shifted[15]), .out(multiplexer_15_out), .sel(Shift_Amount[0]));  // open: en
  Multiplexer multiplexer_16 (
    .in0(Being_Shifted[15]), .in1(Being_Shifted[15]), .out(multiplexer_16_out), .sel(Shift_Amount[0]));  // open: en
  Multiplexer multiplexer_17 (
    .in0(multiplexer_1_out), .in1(multiplexer_3_out), .out(multiplexer_17_out), .sel(Shift_Amount[1]));  // open: en
  Multiplexer multiplexer_18 (
    .in0(multiplexer_2_out), .in1(multiplexer_4_out), .out(multiplexer_18_out), .sel(Shift_Amount[1]));  // open: en
  Multiplexer multiplexer_19 (
    .in0(multiplexer_3_out), .in1(multiplexer_5_out), .out(multiplexer_19_out), .sel(Shift_Amount[1]));  // open: en
  Multiplexer multiplexer_20 (
    .in0(multiplexer_4_out), .in1(multiplexer_6_out), .out(multiplexer_20_out), .sel(Shift_Amount[1]));  // open: en
  Multiplexer multiplexer_21 (
    .in0(multiplexer_5_out), .in1(multiplexer_7_out), .out(multiplexer_21_out), .sel(Shift_Amount[1]));  // open: en
  Multiplexer multiplexer_22 (
    .in0(multiplexer_6_out), .in1(multiplexer_8_out), .out(multiplexer_22_out), .sel(Shift_Amount[1]));  // open: en
  Multiplexer multiplexer_23 (
    .in0(multiplexer_7_out), .in1(multiplexer_9_out), .out(multiplexer_23_out), .sel(Shift_Amount[1]));  // open: en
  Multiplexer multiplexer_24 (
    .in0(multiplexer_8_out), .in1(multiplexer_10_out), .out(multiplexer_24_out), .sel(Shift_Amount[1]));  // open: en
  Multiplexer multiplexer_25 (
    .in0(multiplexer_9_out), .in1(multiplexer_11_out), .out(multiplexer_25_out), .sel(Shift_Amount[1]));  // open: en
  Multiplexer multiplexer_26 (
    .in0(multiplexer_10_out), .in1(multiplexer_12_out), .out(multiplexer_26_out), .sel(Shift_Amount[1]));  // open: en
  Multiplexer multiplexer_27 (
    .in0(multiplexer_11_out), .in1(multiplexer_13_out), .out(multiplexer_27_out), .sel(Shift_Amount[1]));  // open: en
  Multiplexer multiplexer_28 (
    .in0(multiplexer_12_out), .in1(multiplexer_14_out), .out(multiplexer_28_out), .sel(Shift_Amount[1]));  // open: en
  Multiplexer multiplexer_29 (
    .in0(multiplexer_13_out), .in1(multiplexer_15_out), .out(multiplexer_29_out), .sel(Shift_Amount[1]));  // open: en
  Multiplexer multiplexer_30 (
    .in0(multiplexer_14_out), .in1(multiplexer_16_out), .out(multiplexer_30_out), .sel(Shift_Amount[1]));  // open: en
  Multiplexer multiplexer_31 (
    .in0(multiplexer_15_out), .in1(Being_Shifted[15]), .out(multiplexer_31_out), .sel(Shift_Amount[1]));  // open: en
  Multiplexer multiplexer_32 (
    .in0(multiplexer_16_out), .in1(Being_Shifted[15]), .out(multiplexer_32_out), .sel(Shift_Amount[1]));  // open: en
  Multiplexer multiplexer_33 (
    .in0(multiplexer_17_out), .in1(multiplexer_21_out), .out(multiplexer_33_out), .sel(Shift_Amount[2]));  // open: en
  Multiplexer multiplexer_34 (
    .in0(multiplexer_18_out), .in1(multiplexer_22_out), .out(multiplexer_34_out), .sel(Shift_Amount[2]));  // open: en
  Multiplexer multiplexer_35 (
    .in0(multiplexer_19_out), .in1(multiplexer_23_out), .out(multiplexer_35_out), .sel(Shift_Amount[2]));  // open: en
  Multiplexer multiplexer_36 (
    .in0(multiplexer_20_out), .in1(multiplexer_24_out), .out(multiplexer_36_out), .sel(Shift_Amount[2]));  // open: en
  Multiplexer multiplexer_37 (
    .in0(multiplexer_21_out), .in1(multiplexer_25_out), .out(multiplexer_37_out), .sel(Shift_Amount[2]));  // open: en
  Multiplexer multiplexer_38 (
    .in0(multiplexer_22_out), .in1(multiplexer_26_out), .out(multiplexer_38_out), .sel(Shift_Amount[2]));  // open: en
  Multiplexer multiplexer_39 (
    .in0(multiplexer_23_out), .in1(multiplexer_27_out), .out(multiplexer_39_out), .sel(Shift_Amount[2]));  // open: en
  Multiplexer multiplexer_40 (
    .in0(multiplexer_24_out), .in1(multiplexer_28_out), .out(multiplexer_40_out), .sel(Shift_Amount[2]));  // open: en
  Multiplexer multiplexer_41 (
    .in0(multiplexer_25_out), .in1(multiplexer_29_out), .out(multiplexer_41_out), .sel(Shift_Amount[2]));  // open: en
  Multiplexer multiplexer_42 (
    .in0(multiplexer_26_out), .in1(multiplexer_30_out), .out(multiplexer_42_out), .sel(Shift_Amount[2]));  // open: en
  Multiplexer multiplexer_43 (
    .in0(multiplexer_27_out), .in1(multiplexer_31_out), .out(multiplexer_43_out), .sel(Shift_Amount[2]));  // open: en
  Multiplexer multiplexer_44 (
    .in0(multiplexer_28_out), .in1(multiplexer_32_out), .out(multiplexer_44_out), .sel(Shift_Amount[2]));  // open: en
  Multiplexer multiplexer_45 (
    .in0(multiplexer_29_out), .in1(Being_Shifted[15]), .out(multiplexer_45_out), .sel(Shift_Amount[2]));  // open: en
  Multiplexer multiplexer_46 (
    .in0(multiplexer_30_out), .in1(Being_Shifted[15]), .out(multiplexer_46_out), .sel(Shift_Amount[2]));  // open: en
  Multiplexer multiplexer_47 (
    .in0(multiplexer_31_out), .in1(Being_Shifted[15]), .out(multiplexer_47_out), .sel(Shift_Amount[2]));  // open: en
  Multiplexer multiplexer_48 (
    .in0(multiplexer_32_out), .in1(Being_Shifted[15]), .out(multiplexer_48_out), .sel(Shift_Amount[2]));  // open: en
  Multiplexer multiplexer_49 (
    .in0(multiplexer_33_out), .in1(multiplexer_41_out), .out(out_3[0]), .sel(Shift_Amount[3]));  // open: en
  Multiplexer multiplexer_50 (
    .in0(multiplexer_34_out), .in1(multiplexer_42_out), .out(out_3[1]), .sel(Shift_Amount[3]));  // open: en
  Multiplexer multiplexer_51 (
    .in0(multiplexer_35_out), .in1(multiplexer_43_out), .out(out_3[2]), .sel(Shift_Amount[3]));  // open: en
  Multiplexer multiplexer_52 (
    .in0(multiplexer_36_out), .in1(multiplexer_44_out), .out(out_3[3]), .sel(Shift_Amount[3]));  // open: en
  Multiplexer multiplexer_53 (
    .in0(multiplexer_37_out), .in1(multiplexer_45_out), .out(out_3[4]), .sel(Shift_Amount[3]));  // open: en
  Multiplexer multiplexer_54 (
    .in0(multiplexer_38_out), .in1(multiplexer_46_out), .out(out_3[5]), .sel(Shift_Amount[3]));  // open: en
  Multiplexer multiplexer_55 (
    .in0(multiplexer_39_out), .in1(multiplexer_47_out), .out(out_3[6]), .sel(Shift_Amount[3]));  // open: en
  Multiplexer multiplexer_56 (
    .in0(multiplexer_40_out), .in1(multiplexer_48_out), .out(out_3[7]), .sel(Shift_Amount[3]));  // open: en
  Multiplexer multiplexer_57 (
    .in0(multiplexer_41_out), .in1(Being_Shifted[15]), .out(out_3[8]), .sel(Shift_Amount[3]));  // open: en
  Multiplexer multiplexer_58 (
    .in0(multiplexer_42_out), .in1(Being_Shifted[15]), .out(out_3[9]), .sel(Shift_Amount[3]));  // open: en
  Multiplexer multiplexer_59 (
    .in0(multiplexer_43_out), .in1(Being_Shifted[15]), .out(out_3[10]), .sel(Shift_Amount[3]));  // open: en
  Multiplexer multiplexer_60 (
    .in0(multiplexer_44_out), .in1(Being_Shifted[15]), .out(out_3[11]), .sel(Shift_Amount[3]));  // open: en
  Multiplexer multiplexer_61 (
    .in0(multiplexer_45_out), .in1(Being_Shifted[15]), .out(out_3[12]), .sel(Shift_Amount[3]));  // open: en
  Multiplexer multiplexer_62 (
    .in0(multiplexer_46_out), .in1(Being_Shifted[15]), .out(out_3[13]), .sel(Shift_Amount[3]));  // open: en
  Multiplexer multiplexer_63 (
    .in0(multiplexer_47_out), .in1(Being_Shifted[15]), .out(out_3[14]), .sel(Shift_Amount[3]));  // open: en
  Multiplexer multiplexer_64 (
    .in0(multiplexer_48_out), .in1(Being_Shifted[15]), .out(out_3[15]), .sel(Shift_Amount[3]));  // open: en
endmodule

module Shift_Left (
  input  [15:0] Being_Shifted,
  input  [15:0] Shift_Amount,
  output [15:0] out_3
);

  wire multiplexer_1_out, multiplexer_2_out, multiplexer_3_out, multiplexer_4_out, multiplexer_5_out,
       multiplexer_6_out, multiplexer_7_out, multiplexer_8_out, multiplexer_9_out, multiplexer_10_out,
       multiplexer_11_out, multiplexer_12_out, multiplexer_13_out, multiplexer_14_out, multiplexer_15_out,
       multiplexer_16_out, multiplexer_17_out, multiplexer_18_out, multiplexer_19_out, multiplexer_20_out,
       multiplexer_21_out, multiplexer_22_out, multiplexer_23_out, multiplexer_24_out, multiplexer_25_out,
       multiplexer_26_out, multiplexer_27_out, multiplexer_28_out, multiplexer_29_out, multiplexer_30_out,
       multiplexer_31_out, multiplexer_32_out, multiplexer_33_out, multiplexer_34_out, multiplexer_35_out,
       multiplexer_36_out, multiplexer_37_out, multiplexer_38_out, multiplexer_39_out, multiplexer_40_out,
       multiplexer_41_out, multiplexer_42_out, multiplexer_43_out, multiplexer_44_out, multiplexer_45_out,
       multiplexer_46_out, multiplexer_47_out, multiplexer_48_out;

  Multiplexer multiplexer_1 (
    .in0(Being_Shifted[15]), .in1(Being_Shifted[14]), .out(multiplexer_1_out), .sel(Shift_Amount[0]));  // open: en
  Multiplexer multiplexer_2 (
    .in0(Being_Shifted[14]), .in1(Being_Shifted[13]), .out(multiplexer_2_out), .sel(Shift_Amount[0]));  // open: en
  Multiplexer multiplexer_3 (
    .in0(Being_Shifted[13]), .in1(Being_Shifted[12]), .out(multiplexer_3_out), .sel(Shift_Amount[0]));  // open: en
  Multiplexer multiplexer_4 (
    .in0(Being_Shifted[12]), .in1(Being_Shifted[11]), .out(multiplexer_4_out), .sel(Shift_Amount[0]));  // open: en
  Multiplexer multiplexer_5 (
    .in0(Being_Shifted[11]), .in1(Being_Shifted[10]), .out(multiplexer_5_out), .sel(Shift_Amount[0]));  // open: en
  Multiplexer multiplexer_6 (
    .in0(Being_Shifted[10]), .in1(Being_Shifted[9]), .out(multiplexer_6_out), .sel(Shift_Amount[0]));  // open: en
  Multiplexer multiplexer_7 (
    .in0(Being_Shifted[9]), .in1(Being_Shifted[8]), .out(multiplexer_7_out), .sel(Shift_Amount[0]));  // open: en
  Multiplexer multiplexer_8 (
    .in0(Being_Shifted[8]), .in1(Being_Shifted[7]), .out(multiplexer_8_out), .sel(Shift_Amount[0]));  // open: en
  Multiplexer multiplexer_9 (
    .in0(Being_Shifted[7]), .in1(Being_Shifted[6]), .out(multiplexer_9_out), .sel(Shift_Amount[0]));  // open: en
  Multiplexer multiplexer_10 (
    .in0(Being_Shifted[6]), .in1(Being_Shifted[5]), .out(multiplexer_10_out), .sel(Shift_Amount[0]));  // open: en
  Multiplexer multiplexer_11 (
    .in0(Being_Shifted[5]), .in1(Being_Shifted[4]), .out(multiplexer_11_out), .sel(Shift_Amount[0]));  // open: en
  Multiplexer multiplexer_12 (
    .in0(Being_Shifted[4]), .in1(Being_Shifted[3]), .out(multiplexer_12_out), .sel(Shift_Amount[0]));  // open: en
  Multiplexer multiplexer_13 (
    .in0(Being_Shifted[3]), .in1(Being_Shifted[2]), .out(multiplexer_13_out), .sel(Shift_Amount[0]));  // open: en
  Multiplexer multiplexer_14 (
    .in0(Being_Shifted[2]), .in1(Being_Shifted[1]), .out(multiplexer_14_out), .sel(Shift_Amount[0]));  // open: en
  Multiplexer multiplexer_15 (
    .in0(Being_Shifted[1]), .in1(Being_Shifted[0]), .out(multiplexer_15_out), .sel(Shift_Amount[0]));  // open: en
  Multiplexer multiplexer_16 (
    .in0(Being_Shifted[0]), .in1(1'b0), .out(multiplexer_16_out), .sel(Shift_Amount[0]));  // open: en
  Multiplexer multiplexer_17 (
    .in0(multiplexer_1_out), .in1(multiplexer_3_out), .out(multiplexer_17_out), .sel(Shift_Amount[1]));  // open: en
  Multiplexer multiplexer_18 (
    .in0(multiplexer_2_out), .in1(multiplexer_4_out), .out(multiplexer_18_out), .sel(Shift_Amount[1]));  // open: en
  Multiplexer multiplexer_19 (
    .in0(multiplexer_3_out), .in1(multiplexer_5_out), .out(multiplexer_19_out), .sel(Shift_Amount[1]));  // open: en
  Multiplexer multiplexer_20 (
    .in0(multiplexer_4_out), .in1(multiplexer_6_out), .out(multiplexer_20_out), .sel(Shift_Amount[1]));  // open: en
  Multiplexer multiplexer_21 (
    .in0(multiplexer_5_out), .in1(multiplexer_7_out), .out(multiplexer_21_out), .sel(Shift_Amount[1]));  // open: en
  Multiplexer multiplexer_22 (
    .in0(multiplexer_6_out), .in1(multiplexer_8_out), .out(multiplexer_22_out), .sel(Shift_Amount[1]));  // open: en
  Multiplexer multiplexer_23 (
    .in0(multiplexer_7_out), .in1(multiplexer_9_out), .out(multiplexer_23_out), .sel(Shift_Amount[1]));  // open: en
  Multiplexer multiplexer_24 (
    .in0(multiplexer_8_out), .in1(multiplexer_10_out), .out(multiplexer_24_out), .sel(Shift_Amount[1]));  // open: en
  Multiplexer multiplexer_25 (
    .in0(multiplexer_9_out), .in1(multiplexer_11_out), .out(multiplexer_25_out), .sel(Shift_Amount[1]));  // open: en
  Multiplexer multiplexer_26 (
    .in0(multiplexer_10_out), .in1(multiplexer_12_out), .out(multiplexer_26_out), .sel(Shift_Amount[1]));  // open: en
  Multiplexer multiplexer_27 (
    .in0(multiplexer_11_out), .in1(multiplexer_13_out), .out(multiplexer_27_out), .sel(Shift_Amount[1]));  // open: en
  Multiplexer multiplexer_28 (
    .in0(multiplexer_12_out), .in1(multiplexer_14_out), .out(multiplexer_28_out), .sel(Shift_Amount[1]));  // open: en
  Multiplexer multiplexer_29 (
    .in0(multiplexer_13_out), .in1(multiplexer_15_out), .out(multiplexer_29_out), .sel(Shift_Amount[1]));  // open: en
  Multiplexer multiplexer_30 (
    .in0(multiplexer_14_out), .in1(multiplexer_16_out), .out(multiplexer_30_out), .sel(Shift_Amount[1]));  // open: en
  Multiplexer multiplexer_31 (
    .in0(multiplexer_15_out), .in1(1'b0), .out(multiplexer_31_out), .sel(Shift_Amount[1]));  // open: en
  Multiplexer multiplexer_32 (
    .in0(multiplexer_16_out), .in1(1'b0), .out(multiplexer_32_out), .sel(Shift_Amount[1]));  // open: en
  Multiplexer multiplexer_33 (
    .in0(multiplexer_17_out), .in1(multiplexer_21_out), .out(multiplexer_33_out), .sel(Shift_Amount[2]));  // open: en
  Multiplexer multiplexer_34 (
    .in0(multiplexer_18_out), .in1(multiplexer_22_out), .out(multiplexer_34_out), .sel(Shift_Amount[2]));  // open: en
  Multiplexer multiplexer_35 (
    .in0(multiplexer_19_out), .in1(multiplexer_23_out), .out(multiplexer_35_out), .sel(Shift_Amount[2]));  // open: en
  Multiplexer multiplexer_36 (
    .in0(multiplexer_20_out), .in1(multiplexer_24_out), .out(multiplexer_36_out), .sel(Shift_Amount[2]));  // open: en
  Multiplexer multiplexer_37 (
    .in0(multiplexer_21_out), .in1(multiplexer_25_out), .out(multiplexer_37_out), .sel(Shift_Amount[2]));  // open: en
  Multiplexer multiplexer_38 (
    .in0(multiplexer_22_out), .in1(multiplexer_26_out), .out(multiplexer_38_out), .sel(Shift_Amount[2]));  // open: en
  Multiplexer multiplexer_39 (
    .in0(multiplexer_23_out), .in1(multiplexer_27_out), .out(multiplexer_39_out), .sel(Shift_Amount[2]));  // open: en
  Multiplexer multiplexer_40 (
    .in0(multiplexer_24_out), .in1(multiplexer_28_out), .out(multiplexer_40_out), .sel(Shift_Amount[2]));  // open: en
  Multiplexer multiplexer_41 (
    .in0(multiplexer_25_out), .in1(multiplexer_29_out), .out(multiplexer_41_out), .sel(Shift_Amount[2]));  // open: en
  Multiplexer multiplexer_42 (
    .in0(multiplexer_26_out), .in1(multiplexer_30_out), .out(multiplexer_42_out), .sel(Shift_Amount[2]));  // open: en
  Multiplexer multiplexer_43 (
    .in0(multiplexer_27_out), .in1(multiplexer_31_out), .out(multiplexer_43_out), .sel(Shift_Amount[2]));  // open: en
  Multiplexer multiplexer_44 (
    .in0(multiplexer_28_out), .in1(multiplexer_32_out), .out(multiplexer_44_out), .sel(Shift_Amount[2]));  // open: en
  Multiplexer multiplexer_45 (
    .in0(multiplexer_29_out), .in1(1'b0), .out(multiplexer_45_out), .sel(Shift_Amount[2]));  // open: en
  Multiplexer multiplexer_46 (
    .in0(multiplexer_30_out), .in1(1'b0), .out(multiplexer_46_out), .sel(Shift_Amount[2]));  // open: en
  Multiplexer multiplexer_47 (
    .in0(multiplexer_31_out), .in1(1'b0), .out(multiplexer_47_out), .sel(Shift_Amount[2]));  // open: en
  Multiplexer multiplexer_48 (
    .in0(multiplexer_32_out), .in1(1'b0), .out(multiplexer_48_out), .sel(Shift_Amount[2]));  // open: en
  Multiplexer multiplexer_49 (
    .in0(multiplexer_33_out), .in1(multiplexer_41_out), .out(out_3[15]), .sel(Shift_Amount[3]));  // open: en
  Multiplexer multiplexer_50 (
    .in0(multiplexer_34_out), .in1(multiplexer_42_out), .out(out_3[14]), .sel(Shift_Amount[3]));  // open: en
  Multiplexer multiplexer_51 (
    .in0(multiplexer_35_out), .in1(multiplexer_43_out), .out(out_3[13]), .sel(Shift_Amount[3]));  // open: en
  Multiplexer multiplexer_52 (
    .in0(multiplexer_36_out), .in1(multiplexer_44_out), .out(out_3[12]), .sel(Shift_Amount[3]));  // open: en
  Multiplexer multiplexer_53 (
    .in0(multiplexer_37_out), .in1(multiplexer_45_out), .out(out_3[11]), .sel(Shift_Amount[3]));  // open: en
  Multiplexer multiplexer_54 (
    .in0(multiplexer_38_out), .in1(multiplexer_46_out), .out(out_3[10]), .sel(Shift_Amount[3]));  // open: en
  Multiplexer multiplexer_55 (
    .in0(multiplexer_39_out), .in1(multiplexer_47_out), .out(out_3[9]), .sel(Shift_Amount[3]));  // open: en
  Multiplexer multiplexer_56 (
    .in0(multiplexer_40_out), .in1(multiplexer_48_out), .out(out_3[8]), .sel(Shift_Amount[3]));  // open: en
  Multiplexer multiplexer_57 (.in0(multiplexer_41_out), .in1(1'b0), .out(out_3[7]), .sel(Shift_Amount[3]));  // open: en
  Multiplexer multiplexer_58 (.in0(multiplexer_42_out), .in1(1'b0), .out(out_3[6]), .sel(Shift_Amount[3]));  // open: en
  Multiplexer multiplexer_59 (.in0(multiplexer_43_out), .in1(1'b0), .out(out_3[5]), .sel(Shift_Amount[3]));  // open: en
  Multiplexer multiplexer_60 (.in0(multiplexer_44_out), .in1(1'b0), .out(out_3[4]), .sel(Shift_Amount[3]));  // open: en
  Multiplexer multiplexer_61 (.in0(multiplexer_45_out), .in1(1'b0), .out(out_3[3]), .sel(Shift_Amount[3]));  // open: en
  Multiplexer multiplexer_62 (.in0(multiplexer_46_out), .in1(1'b0), .out(out_3[2]), .sel(Shift_Amount[3]));  // open: en
  Multiplexer multiplexer_63 (.in0(multiplexer_47_out), .in1(1'b0), .out(out_3[1]), .sel(Shift_Amount[3]));  // open: en
  Multiplexer multiplexer_64 (.in0(multiplexer_48_out), .in1(1'b0), .out(out_3[0]), .sel(Shift_Amount[3]));  // open: en
endmodule

module FlipSign (
  input  [15:0] in_1,
  output [15:0] out_2
);

  wire [15:0] not_1_out;

  assign not_1_out = ~in_1;  // NOT_Gate not_1, 16 bits wide
  _16_Bit_Adder u_16_bit_adder_1 (.in_1(not_1_out), .in_2(16'h1), .out_3(out_2));
endmodule

module ALU (
  input  [15:0] Left,
  input  [15:0] Right,
  input  [3:0] Selector_Bits,
  input  Enable,
  output [15:0] out_5
);

  wire [15:0] add_long_offset_1_out_3, and_1_out, flipsign_1_out_2, n16_bit_adder_1_out_3,
       n16_bit_adder_2_out_3, n16_bit_adder_3_out_3, not_1_out, or_1_out, shift_left_1_out_3,
       shift_right_1_out_3;

  FlipSign flipsign_1 (.in_1(Right), .out_2(flipsign_1_out_2));
  _16_Bit_Adder u_16_bit_adder_1 (.in_1(Left), .in_2(Right), .out_3(n16_bit_adder_1_out_3));
  _16_Bit_Adder u_16_bit_adder_2 (.in_1(Left), .in_2(flipsign_1_out_2), .out_3(n16_bit_adder_2_out_3));
  assign and_1_out = Left & Right;  // AND_Gate and_1, 16 bits wide
  Shift_Left shift_left_1 (.Being_Shifted(Left), .Shift_Amount(Right), .out_3(shift_left_1_out_3));
  Shift_Right shift_right_1 (.Being_Shifted(Left), .Shift_Amount(Right), .out_3(shift_right_1_out_3));
  assign or_1_out = Left | Right;  // OR_Gate or_1, 16 bits wide
  assign not_1_out = ~Left;  // NOT_Gate not_1, 16 bits wide
  Add_Long_Offset add_long_offset_1 (.In_Left(Left), .In_Right(Right), .out_3(add_long_offset_1_out_3));
  _16_Bit_Adder u_16_bit_adder_3 (.in_1(Left), .in_2(16'h2), .out_3(n16_bit_adder_3_out_3));
  Multiplexer #(.select(4), .width(16)) multiplexer_1 (
    .in0(n16_bit_adder_1_out_3), .in1(n16_bit_adder_2_out_3), .in2(and_1_out), .in3(shift_left_1_out_3),
    .in4(shift_right_1_out_3), .in5(or_1_out), .in6(not_1_out), .in7(add_long_offset_1_out_3),
    .in8(n16_bit_adder_3_out_3), .out(out_5), .sel(Selector_Bits), .en(Enable));  // open: in9, in10, in11, in12, in13, in14, in15

  // Notes on the sheet:
  //   0000: Addition
  //   0001: Subtraction
  //   0010: AND
  //   0011: Shift_Left
  //   0100: Shift_Right
  //   0101: OR
  //   0110: Not Left
  //   0111: Left_Long_Offset + Right
  //   0111: Left + 1
endmodule

module Lookahead_Generator (
  input  P3,
  input  G3,
  input  P2,
  input  G2,
  input  P1,
  input  G1,
  input  P0,
  input  G0,
  input  C_In,
  output out_10,
  output out_11,
  output out_12,
  output out_13
);

  wire and_1_out, and_2_out, and_3_out, and_4_out, and_5_out, and_6_out, and_7_out, and_8_out, and_9_out,
       and_10_out;

  and and_1 (and_1_out, P3, P2, P1, P0, C_In);
  and and_2 (and_2_out, P3, P2, P1, G0);
  and and_3 (and_3_out, P3, P2, G1);
  and and_4 (and_4_out, G2, P3);
  and and_5 (and_5_out, C_In, P0, P1, P2);
  and and_6 (and_6_out, P1, G0, P2);
  and and_7 (and_7_out, P2, G1);
  and and_8 (and_8_out, P0, C_In, P1);
  and and_9 (and_9_out, P1, G0);
  and and_10 (and_10_out, P0, C_In);
  or or_1 (out_10, and_1_out, and_2_out, and_3_out, and_4_out, G3);
  or or_2 (out_11, and_5_out, and_6_out, and_7_out, G2);
  or or_3 (out_12, and_8_out, and_9_out, G1);
  or or_4 (out_13, and_10_out, G0);
endmodule

module _4_Bit_Adder (
  input  [3:0] in_1,
  input  [3:0] in_2,
  input  C_In,
  output C_Out,
  output [3:0] out_5
);

  wire and_1_out, and_2_out, and_3_out, and_4_out, lookahead_generator_1_out_11,
       lookahead_generator_1_out_12, lookahead_generator_1_out_13, xor_1_out, xor_2_out, xor_3_out, xor_4_out;

  and and_1 (and_1_out, in_1[3], in_2[3]);
  and and_2 (and_2_out, in_1[1], in_2[1]);
  and and_3 (and_3_out, in_1[0], in_2[0]);
  xor xor_1 (xor_1_out, in_1[3], in_2[3]);
  xor xor_2 (xor_2_out, in_1[2], in_2[2]);
  and and_4 (and_4_out, in_1[2], in_2[2]);
  xor xor_3 (xor_3_out, in_1[1], in_2[1]);
  xor xor_4 (xor_4_out, in_1[0], in_2[0]);
  Lookahead_Generator lookahead_generator_1 (
    .P3(xor_1_out), .G3(and_1_out), .P2(xor_2_out), .G2(and_4_out), .P1(xor_3_out), .G1(and_2_out),
    .P0(xor_4_out), .G0(and_3_out), .C_In(C_In), .out_10(C_Out), .out_11(lookahead_generator_1_out_11),
    .out_12(lookahead_generator_1_out_12), .out_13(lookahead_generator_1_out_13));
  xor xor_5 (out_5[3], lookahead_generator_1_out_11, xor_1_out);
  xor xor_6 (out_5[2], lookahead_generator_1_out_12, xor_2_out);
  xor xor_7 (out_5[1], lookahead_generator_1_out_13, xor_3_out);
  xor xor_8 (out_5[0], xor_4_out, C_In);
endmodule

module _16_Bit_Adder (
  input  [15:0] in_1,
  input  [15:0] in_2,
  output [15:0] out_3
);

  wire n4_bit_adder_2_c_out, n4_bit_adder_3_c_out, n4_bit_adder_4_c_out;

  _4_Bit_Adder u_4_bit_adder_1 (
    .in_1(in_1[15:12]), .in_2(in_2[15:12]), .C_In(n4_bit_adder_2_c_out), .out_5(out_3[15:12]));  // open: C_Out
  _4_Bit_Adder u_4_bit_adder_2 (
    .in_1(in_1[11:8]), .in_2(in_2[11:8]), .C_In(n4_bit_adder_3_c_out), .C_Out(n4_bit_adder_2_c_out),
    .out_5(out_3[11:8]));
  _4_Bit_Adder u_4_bit_adder_3 (
    .in_1(in_1[7:4]), .in_2(in_2[7:4]), .C_In(n4_bit_adder_4_c_out), .C_Out(n4_bit_adder_3_c_out),
    .out_5(out_3[7:4]));
  _4_Bit_Adder u_4_bit_adder_4 (
    .in_1(in_1[3:0]), .in_2(in_2[3:0]), .C_In(1'b0), .C_Out(n4_bit_adder_4_c_out), .out_5(out_3[3:0]));
endmodule

module Signals (
  input  [3:0] State,
  input  [2:0] Step,
  input  [3:0] Opcode,
  input  [2:0] IR_Rd,
  input  [2:0] IR_RS1,
  input  [2:0] IR_RS2,
  output Read_mm,
  output Write_mm,
  output WMFC,
  output SET_CC,
  output Z_OUT,
  output Z_IN,
  output Y_IN,
  output PSW_OUT,
  output MDR_OUT,
  output MDR_IN,
  output MAR_OUT,
  output MAR_IN,
  output IR_IN,
  output IR_SHORT_OUT,
  output IR_SHIFT_OUT,
  output GPR_OUT,
  output GPR_IN,
  output [2:0] GPR_SEL,
  output [3:0] ALU_SEL
);

  wire and_1_out, and_2_out, and_3_out, and_4_out, and_5_out, and_6_out, and_7_out, and_8_out, and_9_out,
       and_10_out, and_11_out, and_13_out, and_14_out, and_15_out, and_16_out, and_17_out, and_18_out,
       and_19_out, and_20_out, and_21_out, and_22_out, and_23_out, and_24_out, and_25_out, and_26_out,
       and_27_out, and_28_out, and_29_out, and_30_out, and_31_out, and_32_out, and_33_out, and_34_out,
       and_35_out, and_36_out, and_37_out, and_38_out, and_39_out, and_40_out, and_41_out, and_42_out,
       and_43_out, and_44_out, and_45_out, and_46_out, and_47_out, and_48_out, and_49_out, and_50_out,
       and_51_out, and_52_out, and_53_out, and_54_out, and_55_out, and_56_out, decoder_1_out1,
       decoder_1_out4, decoder_1_out5, E_0_5, E_BR, E_CLK_LPSW, E_JSR, E_LOAD, E_NOT, E_RTS, E_ST, Fetch,
       IA_TrapA, IA_TrapB, or_1_out, or_2_out, or_3_out, or_4_out, or_5_out, or_6_out, or_7_out, or_8_out,
       or_9_out, or_10_out, or_11_out, or_12_out, or_13_out, or_14_out, or_15_out, or_16_out, or_17_out,
       or_18_out, or_19_out, or_20_out, or_21_out, or_22_out, or_23_out, or_25_out, or_26_out, or_27_out,
       or_28_out, or_29_out, or_30_out, or_31_out, or_32_out, S_0, S_1, S_2, S_3, S_4, S_5, TTrapA, TTrapB;
  wire [2:0] multiplexer_4_out, multiplexer_7_out;
  wire [3:0] multiplexer_1_out, multiplexer_2_out, multiplexer_3_out, multiplexer_5_out;

  and and_1 (and_1_out, S_2, Fetch);
  and and_2 (and_2_out, S_3, E_LOAD);
  and and_3 (and_3_out, E_0_5, S_1);
  and and_4 (and_4_out, E_0_5, S_3);
  Decoder #(.select(4), .enable("false")) decoder_1 (
    .out0(Fetch), .out1(decoder_1_out1), .out2(IA_TrapA), .out3(IA_TrapB), .out4(decoder_1_out4),
    .out5(decoder_1_out5), .out6(TTrapA), .out7(TTrapB), .out8(E_NOT), .out9(E_BR), .out10(E_ST),
    .out11(E_LOAD), .out12(E_0_5), .out13(E_JSR), .out14(E_RTS), .out15(E_CLK_LPSW), .sel(State));
  Decoder #(.select(3), .enable("false")) decoder_2 (
    .out0(S_0), .out1(S_1), .out2(S_2), .out3(S_3), .out4(S_4), .out5(S_5), .sel(Step));  // open: out6, out7
  or or_1 (or_1_out, TTrapA, IA_TrapA);
  or or_2 (or_2_out, TTrapB, IA_TrapB);
  and and_5 (and_5_out, or_2_out, S_5);
  Multiplexer #(.width(4), .enable("false")) multiplexer_1 (
    .in0(4'b1000), .in1(4'b0111), .out(multiplexer_1_out), .sel(and_1_out));
  Multiplexer #(.width(4), .enable("false")) multiplexer_2 (
    .in0(multiplexer_1_out), .in1(4'b0110), .out(multiplexer_2_out), .sel(and_2_out));
  Multiplexer #(.width(4), .enable("false")) multiplexer_3 (
    .in0(multiplexer_2_out), .in1(4'b0011), .out(multiplexer_3_out), .sel(and_3_out));
  or or_3 (or_3_out, E_LOAD, E_JSR, E_RTS);
  or or_4 (or_4_out, TTrapB, IA_TrapB);
  and and_6 (and_6_out, E_LOAD, S_3);
  or or_5 (or_5_out, TTrapA, TTrapB, IA_TrapB, IA_TrapA);
  or or_6 (or_6_out, S_1, S_3);
  and and_7 (and_7_out, or_1_out, S_4);
  and and_8 (and_8_out, S_3, E_LOAD);
  Multiplexer #(.width(3), .enable("false")) multiplexer_4 (
    .in0(3'b111), .in1(IR_RS2), .out(multiplexer_4_out), .sel(and_9_out));
  and and_9 (and_9_out, S_1, E_0_5);
  Multiplexer #(.width(4), .enable("false")) multiplexer_5 (
    .in0(multiplexer_3_out), .in1(Opcode), .out(multiplexer_5_out), .sel(and_4_out));
  and and_10 (and_10_out, or_3_out, S_1);
  or or_7 (or_7_out, E_NOT, E_BR);
  and and_11 (and_11_out, or_4_out, S_5);
  and and_12 (MAR_OUT, S_2, Fetch);
  or or_8 (or_8_out, E_ST, E_LOAD);
  and and_13 (and_13_out, or_6_out, E_0_5);
  and and_14 (and_14_out, S_1, Fetch);
  or or_9 (or_9_out, E_NOT, E_BR, E_JSR);
  and and_15 (and_15_out, S_3, E_0_5);
  Multiplexer #(.width(4), .enable("false")) multiplexer_6 (
    .in0(multiplexer_5_out), .in1(4'b0000), .out(ALU_SEL), .sel(and_10_out));
  and and_16 (and_16_out, E_ST, S_3);
  and and_17 (and_17_out, S_0, or_7_out);
  and and_18 (and_18_out, E_0_5, S_4);
  and and_19 (and_19_out, S_1, or_10_out);
  or or_10 (or_10_out, Fetch, E_ST, E_LOAD);
  or or_11 (or_11_out, E_0_5, E_JSR, E_RTS);
  and and_20 (and_20_out, Fetch, S_2);
  and and_21 (and_21_out, S_2, E_0_5);
  and and_22 (and_22_out, Fetch, S_1);
  or or_12 (or_12_out, E_CLK_LPSW, TTrapB, IA_TrapB);
  and and_23 (and_23_out, S_1, or_8_out);
  and and_24 (and_24_out, S_3, or_5_out);
  or or_13 (or_13_out, E_JSR, E_RTS);
  and and_25 (and_25_out, E_0_5, S_4);
  and and_26 (and_26_out, or_9_out, S_0);
  Multiplexer #(.width(3), .enable("false")) multiplexer_7 (
    .in0(multiplexer_4_out), .in1(IR_RS1), .out(multiplexer_7_out), .sel(and_15_out));
  and and_27 (and_27_out, Fetch, S_0);
  or or_14 (or_14_out, IA_TrapA, TTrapA);
  and and_28 (and_28_out, or_14_out, S_1);
  and and_29 (and_29_out, S_4, or_15_out);
  or or_15 (or_15_out, IA_TrapA, TTrapA);
  or or_16 (or_16_out, IA_TrapA, TTrapA);
  and and_30 (and_30_out, S_2, or_11_out);
  or or_17 (or_17_out, E_LOAD, E_0_5);
  and and_31 (and_31_out, S_2, or_12_out);
  and and_32 (and_32_out, E_ST, S_2);
  and and_33 (and_33_out, or_13_out, S_1);
  and and_34 (and_34_out, S_2, E_ST);
  and and_35 (and_35_out, S_2, E_ST);
  or or_18 (or_18_out, TTrapB, IA_TrapB);
  or or_19 (or_19_out, S_2, S_5);
  and and_36 (and_36_out, E_LOAD, S_2);
  or or_20 (or_20_out, E_JSR, E_RTS, E_CLK_LPSW);
  or or_21 (or_21_out, E_ST, E_LOAD);
  or or_22 (or_22_out, E_CLK_LPSW, E_BR, E_NOT);
  and and_37 (and_37_out, or_17_out, S_3);
  or or_23 (or_23_out, E_0_5, E_RTS);
  and and_38 (and_38_out, or_23_out, S_0);
  or or_24 (MDR_OUT, and_31_out, and_11_out, and_6_out);
  or or_25 (or_25_out, S_4, S_1);
  or or_26 (or_26_out, Fetch, E_CLK_LPSW, or_5_out);
  or or_27 (or_27_out, E_LOAD, E_ST);
  or or_28 (or_28_out, Fetch, E_JSR, E_RTS);
  or or_29 (or_29_out, E_JSR, E_RTS);
  or or_30 (or_30_out, E_NOT, E_JSR, E_RTS);
  and and_39 (and_39_out, or_30_out, S_0);
  Multiplexer #(.width(3), .enable("false")) multiplexer_8 (
    .in0(multiplexer_7_out), .in1(IR_Rd), .out(GPR_SEL), .sel(or_32_out));
  and and_40 (and_40_out, E_LOAD, S_1);
  and and_41 (and_41_out, or_18_out, S_0);
  and and_42 (and_42_out, E_CLK_LPSW, S_0);
  and and_43 (and_43_out, E_ST, S_2);
  and and_44 (and_44_out, or_19_out, or_16_out);
  and and_45 (and_45_out, Fetch, S_1);
  and and_46 (and_46_out, S_1, E_CLK_LPSW);
  and and_47 (and_47_out, S_2, or_20_out);
  and and_48 (and_48_out, S_3, or_21_out);
  and and_49 (and_49_out, S_0, or_22_out);
  and and_50 (and_50_out, or_11_out, S_1);
  and and_51 (and_51_out, or_10_out, S_0);
  or or_31 (or_31_out, IA_TrapA, TTrapA);
  and and_52 (and_52_out, or_31_out, or_25_out);
  and and_53 (and_53_out, S_0, or_26_out);
  and and_54 (and_54_out, or_27_out, S_0);
  and and_55 (and_55_out, or_28_out, S_0);
  and and_56 (and_56_out, or_29_out, S_2);
  or or_32 (or_32_out, and_39_out, and_25_out, and_8_out, and_35_out);
  or or_33 (Read_mm, and_27_out, and_40_out, and_41_out, and_42_out);
  or or_34 (Write_mm, and_28_out, and_29_out, and_43_out);
  or or_35 (WMFC, and_44_out, and_45_out, and_36_out, and_16_out, and_46_out);
  or or_36 (SET_CC, and_47_out, and_17_out, and_48_out, and_18_out);
  or or_37 (Z_OUT, and_18_out, and_49_out, and_19_out, and_30_out);
  or or_38 (Z_IN, and_50_out, and_37_out, and_20_out, and_51_out);
  or or_39 (Y_IN, and_38_out, and_22_out, and_21_out);
  and and_57 (PSW_OUT, S_1, or_31_out);
  or or_40 (MDR_IN, and_52_out, and_32_out);
  or or_41 (MAR_IN, and_53_out, and_23_out, and_24_out);
  and and_58 (IR_IN, Fetch, S_2);
  or or_42 (IR_SHORT_OUT, and_54_out, and_33_out);
  and and_59 (IR_SHIFT_OUT, S_0, E_0_5);
  or or_43 (GPR_OUT, and_55_out, and_13_out, and_34_out, and_7_out);
  or or_44 (GPR_IN, and_14_out, and_25_out, and_8_out, and_26_out, and_56_out, and_5_out);
endmodule
