// Logisim project Starting.circ as structural Verilog: 16 circuits, main circuit main
module main (
);

  ALU alu_1 ();  // open: Left, Right, Selector_Bits, Enable, out_5
endmodule

module XOR (
  input  A,
  input  B,
  output Output
);

  wire and_1_out, not_1_out, or_1_out;

  and and_1 (and_1_out, A, B);
  or or_1 (or_1_out, B, A);
  not not_1 (not_1_out, and_1_out);
  and and_2 (Output, not_1_out, or_1_out);
endmodule

module Adder_1_Bit (
  input  IN_Left,
  input  IN_Right,
  input  C_IN,
  output OUT,
  output C_OUT
);

  wire and_1_out, and_2_out, not_1_out, or_1_out, xor_1_output;

  XOR xor_1 (.A(IN_Left), .B(IN_Right), .Output(xor_1_output));
  not not_1 (not_1_out, C_IN);
  and and_1 (and_1_out, IN_Right, not_1_out, IN_Left);
  or or_1 (or_1_out, IN_Left, IN_Right);
  and and_2 (and_2_out, or_1_out, C_IN);
  or or_2 (C_OUT, and_1_out, and_2_out);
  XOR xor_2 (.A(xor_1_output), .B(C_IN), .Output(OUT));
endmodule

module Adder (
  input  [15:0] in_1,
  input  [15:0] in_2,
  output [15:0] out_3
);

  wire adder_1_bit_2_c_out, adder_1_bit_3_c_out, adder_1_bit_4_c_out, adder_1_bit_5_c_out,
       adder_1_bit_6_c_out, adder_1_bit_7_c_out, adder_1_bit_8_c_out, adder_1_bit_9_c_out,
       adder_1_bit_10_c_out, adder_1_bit_11_c_out, adder_1_bit_12_c_out, adder_1_bit_13_c_out,
       adder_1_bit_14_c_out, adder_1_bit_15_c_out, adder_1_bit_16_c_out;

  Adder_1_Bit adder_1_bit_1 (
    .IN_Left(in_1[15]), .IN_Right(in_2[15]), .C_IN(adder_1_bit_2_c_out), .OUT(out_3[15]));  // open: C_OUT
  Adder_1_Bit adder_1_bit_2 (
    .IN_Left(in_1[14]), .IN_Right(in_2[14]), .C_IN(adder_1_bit_3_c_out), .OUT(out_3[14]),
    .C_OUT(adder_1_bit_2_c_out));
  Adder_1_Bit adder_1_bit_3 (
    .IN_Left(in_1[13]), .IN_Right(in_2[13]), .C_IN(adder_1_bit_4_c_out), .OUT(out_3[13]),
    .C_OUT(adder_1_bit_3_c_out));
  Adder_1_Bit adder_1_bit_4 (
    .IN_Left(in_1[12]), .IN_Right(in_2[12]), .C_IN(adder_1_bit_5_c_out), .OUT(out_3[12]),
    .C_OUT(adder_1_bit_4_c_out));
  Adder_1_Bit adder_1_bit_5 (
    .IN_Left(in_1[11]), .IN_Right(in_2[11]), .C_IN(adder_1_bit_6_c_out), .OUT(out_3[11]),
    .C_OUT(adder_1_bit_5_c_out));
  Adder_1_Bit adder_1_bit_6 (
    .IN_Left(in_1[10]), .IN_Right(in_2[10]), .C_IN(adder_1_bit_7_c_out), .OUT(out_3[10]),
    .C_OUT(adder_1_bit_6_c_out));
  Adder_1_Bit adder_1_bit_7 (
    .IN_Left(in_1[9]), .IN_Right(in_2[9]), .C_IN(adder_1_bit_8_c_out), .OUT(out_3[9]),
    .C_OUT(adder_1_bit_7_c_out));
  Adder_1_Bit adder_1_bit_8 (
    .IN_Left(in_1[8]), .IN_Right(in_2[8]), .C_IN(adder_1_bit_9_c_out), .OUT(out_3[8]),
    .C_OUT(adder_1_bit_8_c_out));
  Adder_1_Bit adder_1_bit_9 (
    .IN_Left(in_1[7]), .IN_Right(in_2[7]), .C_IN(adder_1_bit_10_c_out), .OUT(out_3[7]),
    .C_OUT(adder_1_bit_9_c_out));
  Adder_1_Bit adder_1_bit_10 (
    .IN_Left(in_1[6]), .IN_Right(in_2[6]), .C_IN(adder_1_bit_11_c_out), .OUT(out_3[6]),
    .C_OUT(adder_1_bit_10_c_out));
  Adder_1_Bit adder_1_bit_11 (
    .IN_Left(in_1[5]), .IN_Right(in_2[5]), .C_IN(adder_1_bit_12_c_out), .OUT(out_3[5]),
    .C_OUT(adder_1_bit_11_c_out));
  Adder_1_Bit adder_1_bit_12 (
    .IN_Left(in_1[4]), .IN_Right(in_2[4]), .C_IN(adder_1_bit_13_c_out), .OUT(out_3[4]),
    .C_OUT(adder_1_bit_12_c_out));
  Adder_1_Bit adder_1_bit_13 (
    .IN_Left(in_1[3]), .IN_Right(in_2[3]), .C_IN(adder_1_bit_14_c_out), .OUT(out_3[3]),
    .C_OUT(adder_1_bit_13_c_out));
  Adder_1_Bit adder_1_bit_14 (
    .IN_Left(in_1[2]), .IN_Right(in_2[2]), .C_IN(adder_1_bit_15_c_out), .OUT(out_3[2]),
    .C_OUT(adder_1_bit_14_c_out));
  Adder_1_Bit adder_1_bit_15 (
    .IN_Left(in_1[1]), .IN_Right(in_2[1]), .C_IN(adder_1_bit_16_c_out), .OUT(out_3[1]),
    .C_OUT(adder_1_bit_15_c_out));
  Adder_1_Bit adder_1_bit_16 (
    .IN_Left(in_1[0]), .IN_Right(in_2[0]), .C_IN(1'b0), .OUT(out_3[0]), .C_OUT(adder_1_bit_16_c_out));

  // Notes on the sheet:
  //   Highest Bit
  //   Lowest Bit
endmodule

module ALU (
  input  [15:0] Left,
  input  [15:0] Right,
  input  [3:0] Selector_Bits,
  input  Enable,
  output [15:0] out_5
);

  wire [15:0] add_long_offset_1_out_3, adder_1_out_3, and_1_out, flipsign_1_out_2, n16_bit_adder_1_out_3,
       n16_bit_adder_2_out_3, not_1_out, or_1_out, shift_left_1_out_3, shift_right_1_out_3;

  FlipSign flipsign_1 (.in_1(Right), .out_2(flipsign_1_out_2));
  _16_Bit_Adder u_16_bit_adder_1 (.in_1(Left), .in_2(Right), .out_3(n16_bit_adder_1_out_3));
  _16_Bit_Adder u_16_bit_adder_2 (.in_1(Left), .in_2(flipsign_1_out_2), .out_3(n16_bit_adder_2_out_3));
  assign and_1_out = Left & Right;  // AND_Gate and_1, 16 bits wide
  Shift_Left shift_left_1 (.Being_Shifted(Left), .Shift_Amount(Right), .out_3(shift_left_1_out_3));
  Shift_Right shift_right_1 (.Being_Shifted(Left), .Shift_Amount(Right), .out_3(shift_right_1_out_3));
  assign or_1_out = Left | Right;  // OR_Gate or_1, 16 bits wide
  assign not_1_out = ~Left;  // NOT_Gate not_1, 16 bits wide
  Add_Long_Offset add_long_offset_1 (.In_Left(Left), .In_Right(Right), .out_3(add_long_offset_1_out_3));
  Adder adder_1 (.in_1(Left), .in_2(16'h1), .out_3(adder_1_out_3));
  Multiplexer #(.select(4), .width(16)) multiplexer_1 (
    .in0(n16_bit_adder_1_out_3), .in1(n16_bit_adder_2_out_3), .in2(and_1_out), .in3(shift_left_1_out_3),
    .in4(shift_right_1_out_3), .in5(or_1_out), .in6(not_1_out), .in7(add_long_offset_1_out_3),
    .in8(adder_1_out_3), .out(out_5), .sel(Selector_Bits), .en(Enable));  // open: in9, in10, in11, in12, in13, in14, in15

  // Notes on the sheet:
  //   0000: Addition
  //   0001: Subtraction
  //   0010: AND
  //   0011: Shift_Left
  //   0100: Shift_Right
  //   0101: OR
  //   0110: Not Left
  //   0111: Left_Long_Offset + Right
  //   0111: Left + 1
endmodule

module FlipSign (
  input  [15:0] in_1,
  output [15:0] out_2
);

  wire [15:0] not_1_out;

  assign not_1_out = ~in_1;  // NOT_Gate not_1, 16 bits wide
  Adder adder_1 (.in_1(not_1_out), .in_2(16'h1), .out_3(out_2));
endmodule

module Shift_Left (
  input  [15:0] Being_Shifted,
  input  [15:0] Shift_Amount,
  output [15:0] out_3
);

  wire multiplexer_1_out, multiplexer_2_out, multiplexer_3_out, multiplexer_4_out, multiplexer_5_out,
       multiplexer_6_out, multiplexer_7_out, multiplexer_8_out, multiplexer_9_out, multiplexer_10_out,
       multiplexer_11_out, multiplexer_12_out, multiplexer_13_out, multiplexer_14_out, multiplexer_15_out,
       multiplexer_16_out, multiplexer_17_out, multiplexer_18_out, multiplexer_19_out, multiplexer_20_out,
       multiplexer_21_out, multiplexer_22_out, multiplexer_23_out, multiplexer_24_out, multiplexer_25_out,
       multiplexer_26_out, multiplexer_27_out, multiplexer_28_out, multiplexer_29_out, multiplexer_30_out,
       multiplexer_31_out, multiplexer_32_out, multiplexer_33_out, multiplexer_34_out, multiplexer_35_out,
       multiplexer_36_out, multiplexer_37_out, multiplexer_38_out, multiplexer_39_out, multiplexer_40_out,
       multiplexer_41_out, multiplexer_42_out, multiplexer_43_out, multiplexer_44_out, multiplexer_45_out,
       multiplexer_46_out, multiplexer_47_out, multiplexer_48_out;

  Multiplexer multiplexer_1 (
    .in0(Being_Shifted[15]), .in1(Being_Shifted[14]), .out(multiplexer_1_out), .sel(Shift_Amount[0]));  // open: en
  Multiplexer multiplexer_2 (
    .in0(Being_Shifted[14]), .in1(Being_Shifted[13]), .out(multiplexer_2_out), .sel(Shift_Amount[0]));  // open: en
  Multiplexer multiplexer_3 (
    .in0(Being_Shifted[13]), .in1(Being_Shifted[12]), .out(multiplexer_3_out), .sel(Shift_Amount[0]));  // open: en
  Multiplexer multiplexer_4 (
    .in0(Being_Shifted[12]), .in1(Being_Shifted[11]), .out(multiplexer_4_out), .sel(Shift_Amount[0]));  // open: en
  Multiplexer multiplexer_5 (
    .in0(Being_Shifted[11]), .in1(Being_Shifted[10]), .out(multiplexer_5_out), .sel(Shift_Amount[0]));  // open: en
  Multiplexer multiplexer_6 (
    .in0(Being_Shifted[10]), .in1(Being_Shifted[9]), .out(multiplexer_6_out), .sel(Shift_Amount[0]));  // open: en
  Multiplexer multiplexer_7 (
    .in0(Being_Shifted[9]), .in1(Being_Shifted[8]), .out(multiplexer_7_out), .sel(Shift_Amount[0]));  // open: en
  Multiplexer multiplexer_8 (
    .in0(Being_Shifted[8]), .in1(Being_Shifted[7]), .out(multiplexer_8_out), .sel(Shift_Amount[0]));  // open: en
  Multiplexer multiplexer_9 (
    .in0(Being_Shifted[7]), .in1(Being_Shifted[6]), .out(multiplexer_9_out), .sel(Shift_Amount[0]));  // open: en
  Multiplexer multiplexer_10 (
    .in0(Being_Shifted[6]), .in1(Being_Shifted[5]), .out(multiplexer_10_out), .sel(Shift_Amount[0]));  // open: en
  Multiplexer multiplexer_11 (
    .in0(Being_Shifted[5]), .in1(Being_Shifted[4]), .out(multiplexer_11_out), .sel(Shift_Amount[0]));  // open: en
  Multiplexer multiplexer_12 (
    .in0(Being_Shifted[4]), .in1(Being_Shifted[3]), .out(multiplexer_12_out), .sel(Shift_Amount[0]));  // open: en
  Multiplexer multiplexer_13 (
    .in0(Being_Shifted[3]), .in1(Being_Shifted[2]), .out(multiplexer_13_out), .sel(Shift_Amount[0]));  // open: en
  Multiplexer multiplexer_14 (
    .in0(Being_Shifted[2]), .in1(Being_Shifted[1]), .out(multiplexer_14_out), .sel(Shift_Amount[0]));  // open: en
  Multiplexer multiplexer_15 (
    .in0(Being_Shifted[1]), .in1(Being_Shifted[0]), .out(multiplexer_15_out), .sel(Shift_Amount[0]));  // open: en
  Multiplexer multiplexer_16 (
    .in0(Being_Shifted[0]), .in1(1'b0), .out(multiplexer_16_out), .sel(Shift_Amount[0]));  // open: en
  Multiplexer multiplexer_17 (
    .in0(multiplexer_1_out), .in1(multiplexer_3_out), .out(multiplexer_17_out), .sel(Shift_Amount[1]));  // open: en
  Multiplexer multiplexer_18 (
    .in0(multiplexer_2_out), .in1(multiplexer_4_out), .out(multiplexer_18_out), .sel(Shift_Amount[1]));  // open: en
  Multiplexer multiplexer_19 (
    .in0(multiplexer_3_out), .in1(multiplexer_5_out), .out(multiplexer_19_out), .sel(Shift_Amount[1]));  // open: en
  Multiplexer multiplexer_20 (
    .in0(multiplexer_4_out), .in1(multiplexer_6_out), .out(multiplexer_20_out), .sel(Shift_Amount[1]));  // open: en
  Multiplexer multiplexer_21 (
    .in0(multiplexer_5_out), .in1(multiplexer_7_out), .out(multiplexer_21_out), .sel(Shift_Amount[1]));  // open: en
  Multiplexer multiplexer_22 (
    .in0(multiplexer_6_out), .in1(multiplexer_8_out), .out(multiplexer_22_out), .sel(Shift_Amount[1]));  // open: en
  Multiplexer multiplexer_23 (
    .in0(multiplexer_7_out), .in1(multiplexer_9_out), .out(multiplexer_23_out), .sel(Shift_Amount[1]));  // open: en
  Multiplexer multiplexer_24 (
    .in0(multiplexer_8_out), .in1(multiplexer_10_out), .out(multiplexer_24_out), .sel(Shift_Amount[1]));  // open: en
  Multiplexer multiplexer_25 (
    .in0(multiplexer_9_out), .in1(multiplexer_11_out), .out(multiplexer_25_out), .sel(Shift_Amount[1]));  // open: en
  Multiplexer multiplexer_26 (
    .in0(multiplexer_10_out), .in1(multiplexer_12_out), .out(multiplexer_26_out), .sel(Shift_Amount[1]));  // open: en
  Multiplexer multiplexer_27 (
    .in0(multiplexer_11_out), .in1(multiplexer_13_out), .out(multiplexer_27_out), .sel(Shift_Amount[1]));  // open: en
  Multiplexer multiplexer_28 (
    .in0(multiplexer_12_out), .in1(multiplexer_14_out), .out(multiplexer_28_out), .sel(Shift_Amount[1]));  // open: en
  Multiplexer multiplexer_29 (
    .in0(multiplexer_13_out), .in1(multiplexer_15_out), .out(multiplexer_29_out), .sel(Shift_Amount[1]));  // open: en
  Multiplexer multiplexer_30 (
    .in0(multiplexer_14_out), .in1(multiplexer_16_out), .out(multiplexer_30_out), .sel(Shift_Amount[1]));  // open: en
  Multiplexer multiplexer_31 (
    .in0(multiplexer_15_out), .in1(1'b0), .out(multiplexer_31_out), .sel(Shift_Amount[1]));  // open: en
  Multiplexer multiplexer_32 (
    .in0(multiplexer_16_out), .in1(1'b0), .out(multiplexer_32_out), .sel(Shift_Amount[1]));  // open: en
  Multiplexer multiplexer_33 (
    .in0(multiplexer_17_out), .in1(multiplexer_21_out), .out(multiplexer_33_out), .sel(Shift_Amount[2]));  // open: en
  Multiplexer multiplexer_34 (
    .in0(multiplexer_18_out), .in1(multiplexer_22_out), .out(multiplexer_34_out), .sel(Shift_Amount[2]));  // open: en
  Multiplexer multiplexer_35 (
    .in0(multiplexer_19_out), .in1(multiplexer_23_out), .out(multiplexer_35_out), .sel(Shift_Amount[2]));  // open: en
  Multiplexer multiplexer_36 (
    .in0(multiplexer_20_out), .in1(multiplexer_24_out), .out(multiplexer_36_out), .sel(Shift_Amount[2]));  // open: en
  Multiplexer multiplexer_37 (
    .in0(multiplexer_21_out), .in1(multiplexer_25_out), .out(multiplexer_37_out), .sel(Shift_Amount[2]));  // open: en
  Multiplexer multiplexer_38 (
    .in0(multiplexer_22_out), .in1(multiplexer_26_out), .out(multiplexer_38_out), .sel(Shift_Amount[2]));  // open: en
  Multiplexer multiplexer_39 (
    .in0(multiplexer_23_out), .in1(multiplexer_27_out), .out(multiplexer_39_out), .sel(Shift_Amount[2]));  // open: en
  Multiplexer multiplexer_40 (
    .in0(multiplexer_24_out), .in1(multiplexer_28_out), .out(multiplexer_40_out), .sel(Shift_Amount[2]));  // open: en
  Multiplexer multiplexer_41 (
    .in0(multiplexer_25_out), .in1(multiplexer_29_out), .out(multiplexer_41_out), .sel(Shift_Amount[2]));  // open: en
  Multiplexer multiplexer_42 (
    .in0(multiplexer_26_out), .in1(multiplexer_30_out), .out(multiplexer_42_out), .sel(Shift_Amount[2]));  // open: en
  Multiplexer multiplexer_43 (
    .in0(multiplexer_27_out), .in1(multiplexer_31_out), .out(multiplexer_43_out), .sel(Shift_Amount[2]));  // open: en
  Multiplexer multiplexer_44 (
    .in0(multiplexer_28_out), .in1(multiplexer_32_out), .out(multiplexer_44_out), .sel(Shift_Amount[2]));  // open: en
  Multiplexer multiplexer_45 (
    .in0(multiplexer_29_out), .in1(1'b0), .out(multiplexer_45_out), .sel(Shift_Amount[2]));  // open: en
  Multiplexer multiplexer_46 (
    .in0(multiplexer_30_out), .in1(1'b0), .out(multiplexer_46_out), .sel(Shift_Amount[2]));  // open: en
  Multiplexer multiplexer_47 (
    .in0(multiplexer_31_out), .in1(1'b0), .out(multiplexer_47_out), .sel(Shift_Amount[2]));  // open: en
  Multiplexer multiplexer_48 (
    .in0(multiplexer_32_out), .in1(1'b0), .out(multiplexer_48_out), .sel(Shift_Amount[2]));  // open: en
  Multiplexer multiplexer_49 (
    .in0(multiplexer_33_out), .in1(multiplexer_41_out), .out(out_3[15]), .sel(Shift_Amount[3]));  // open: en
  Multiplexer multiplexer_50 (
    .in0(multiplexer_34_out), .in1(multiplexer_42_out), .out(out_3[14]), .sel(Shift_Amount[3]));  // open: en
  Multiplexer multiplexer_51 (
    .in0(multiplexer_35_out), .in1(multiplexer_43_out), .out(out_3[13]), .sel(Shift_Amount[3]));  // open: en
  Multiplexer multiplexer_52 (
    .in0(multiplexer_36_out), .in1(multiplexer_44_out), .out(out_3[12]), .sel(Shift_Amount[3]));  // open: en
  Multiplexer multiplexer_53 (
    .in0(multiplexer_37_out), .in1(multiplexer_45_out), .out(out_3[11]), .sel(Shift_Amount[3]));  // open: en
  Multiplexer multiplexer_54 (
    .in0(multiplexer_38_out), .in1(multiplexer_46_out), .out(out_3[10]), .sel(Shift_Amount[3]));  // open: en
  Multiplexer multiplexer_55 (
    .in0(multiplexer_39_out), .in1(multiplexer_47_out), .out(out_3[9]), .sel(Shift_Amount[3]));  // open: en
  Multiplexer multiplexer_56 (
    .in0(multiplexer_40_out), .in1(multiplexer_48_out), .out(out_3[8]), .sel(Shift_Amount[3]));  // open: en
  Multiplexer multiplexer_57 (.in0(multiplexer_41_out), .in1(1'b0), .out(out_3[7]), .sel(Shift_Amount[3]));  // open: en
  Multiplexer multiplexer_58 (.in0(multiplexer_42_out), .in1(1'b0), .out(out_3[6]), .sel(Shift_Amount[3]));  // open: en
  Multiplexer multiplexer_59 (.in0(multiplexer_43_out), .in1(1'b0), .out(out_3[5]), .sel(Shift_Amount[3]));  // open: en
  Multiplexer multiplexer_60 (.in0(multiplexer_44_out), .in1(1'b0), .out(out_3[4]), .sel(Shift_Amount[3]));  // open: en
  Multiplexer multiplexer_61 (.in0(multiplexer_45_out), .in1(1'b0), .out(out_3[3]), .sel(Shift_Amount[3]));  // open: en
  Multiplexer multiplexer_62 (.in0(multiplexer_46_out), .in1(1'b0), .out(out_3[2]), .sel(Shift_Amount[3]));  // open: en
  Multiplexer multiplexer_63 (.in0(multiplexer_47_out), .in1(1'b0), .out(out_3[1]), .sel(Shift_Amount[3]));  // open: en
  Multiplexer multiplexer_64 (.in0(multiplexer_48_out), .in1(1'b0), .out(out_3[0]), .sel(Shift_Amount[3]));  // open: en
endmodule

module Shift_Right (
  input  [15:0] Being_Shifted,
  input  [15:0] Shift_Amount,
  output [15:0] out_3
);

  wire multiplexer_1_out, multiplexer_2_out, multiplexer_3_out, multiplexer_4_out, multiplexer_5_out,
       multiplexer_6_out, multiplexer_7_out, multiplexer_8_out, multiplexer_9_out, multiplexer_10_out,
       multiplexer_11_out, multiplexer_12_out, multiplexer_13_out, multiplexer_14_out, multiplexer_15_out,
       multiplexer_16_out, multiplexer_17_out, multiplexer_18_out, multiplexer_19_out, multiplexer_20_out,
       multiplexer_21_out, multiplexer_22_out, multiplexer_23_out, multiplexer_24_out, multiplexer_25_out,
       multiplexer_26_out, multiplexer_27_out, multiplexer_28_out, multiplexer_29_out, multiplexer_30_out,
       multiplexer_31_out, multiplexer_32_out, multiplexer_33_out, multiplexer_34_out, multiplexer_35_out,
       multiplexer_36_out, multiplexer_37_out, multiplexer_38_out, multiplexer_39_out, multiplexer_40_out,
       multiplexer_41_out, multiplexer_42_out, multiplexer_43_out, multiplexer_44_out, multiplexer_45_out,
       multiplexer_46_out, multiplexer_47_out, multiplexer_48_out;

  Multiplexer multiplexer_1 (
    .in0(Being_Shifted[0]), .in1(Being_Shifted[1]), .out(multiplexer_1_out), .sel(Shift_Amount[0]));  // open: en
  Multiplexer multiplexer_2 (
    .in0(Being_Shifted[1]), .in1(Being_Shifted[2]), .out(multiplexer_2_out), .sel(Shift_Amount[0]));  // open: en
  Multiplexer multiplexer_3 (
    .in0(Being_Shifted[2]), .in1(Being_Shifted[3]), .out(multiplexer_3_out), .sel(Shift_Amount[0]));  // open: en
  Multiplexer multiplexer_4 (
    .in0(Being_Shifted[3]), .in1(Being_Shifted[4]), .out(multiplexer_4_out), .sel(Shift_Amount[0]));  // open: en
  Multiplexer multiplexer_5 (
    .in0(Being_Shifted[4]), .in1(Being_Shifted[5]), .out(multiplexer_5_out), .sel(Shift_Amount[0]));  // open: en
  Multiplexer multiplexer_6 (
    .in0(Being_Shifted[5]), .in1(Being_Shifted[6]), .out(multiplexer_6_out), .sel(Shift_Amount[0]));  // open: en
  Multiplexer multiplexer_7 (
    .in0(Being_Shifted[6]), .in1(Being_Shifted[7]), .out(multiplexer_7_out), .sel(Shift_Amount[0]));  // open: en
  Multiplexer multiplexer_8 (
    .in0(Being_Shifted[7]), .in1(Being_Shifted[8]), .out(multiplexer_8_out), .sel(Shift_Amount[0]));  // open: en
  Multiplexer multiplexer_9 (
    .in0(Being_Shifted[8]), .in1(Being_Shifted[9]), .out(multiplexer_9_out), .sel(Shift_Amount[0]));  // open: en
  Multiplexer multiplexer_10 (
    .in0(Being_Shifted[9]), .in1(Being_Shifted[10]), .out(multiplexer_10_out), .sel(Shift_Amount[0]));  // open: en
  Multiplexer multiplexer_11 (
    .in0(Being_Shifted[10]), .in1(Being_Shifted[11]), .out(multiplexer_11_out), .sel(Shift_Amount[0]));  // open: en
  Multiplexer multiplexer_12 (
    .in0(Being_Shifted[11]), .in1(Being_Shifted[12]), .out(multiplexer_12_out), .sel(Shift_Amount[0]));  // open: en
  Multiplexer multiplexer_13 (
    .in0(Being_Shifted[12]), .in1(Being_Shifted[13]), .out(multiplexer_13_out), .sel(Shift_Amount[0]));  // open: en
  Multiplexer multiplexer_14 (
    .in0(Being_Shifted[13]), .in1(Being_Shifted[14]), .out(multiplexer_14_out), .sel(Shift_Amount[0]));  // open: en
  Multiplexer multiplexer_15 (
    .in0(Being_Shifted[14]), .in1(Being_Shifted[15]), .out(multiplexer_15_out), .sel(Shift_Amount[0]));  // open: en
  Multiplexer multiplexer_16 (
    .in0(Being_Shifted[15]), .in1(Being_Shifted[15]), .out(multiplexer_16_out), .sel(Shift_Amount[0]));  // open: en
  Multiplexer multiplexer_17 (
    .in0(multiplexer_1_out), .in1(multiplexer_3_out), .out(multiplexer_17_out), .sel(Shift_Amount[1]));  // open: en
  Multiplexer multiplexer_18 (
    .in0(multiplexer_2_out), .in1(multiplexer_4_out), .out(multiplexer_18_out), .sel(Shift_Amount[1]));  // open: en
  Multiplexer multiplexer_19 (
    .in0(multiplexer_3_out), .in1(multiplexer_5_out), .out(multiplexer_19_out), .sel(Shift_Amount[1]));  // open: en
  Multiplexer multiplexer_20 (
    .in0(multiplexer_4_out), .in1(multiplexer_6_out), .out(multiplexer_20_out), .sel(Shift_Amount[1]));  // open: en
  Multiplexer multiplexer_21 (
    .in0(multiplexer_5_out), .in1(multiplexer_7_out), .out(multiplexer_21_out), .sel(Shift_Amount[1]));  // open: en
  Multiplexer multiplexer_22 (
    .in0(multiplexer_6_out), .in1(multiplexer_8_out), .out(multiplexer_22_out), .sel(Shift_Amount[1]));  // open: en
  Multiplexer multiplexer_23 (
    .in0(multiplexer_7_out), .in1(multiplexer_9_out), .out(multiplexer_23_out), .sel(Shift_Amount[1]));  // open: en
  Multiplexer multiplexer_24 (
    .in0(multiplexer_8_out), .in1(multiplexer_10_out), .out(multiplexer_24_out), .sel(Shift_Amount[1]));  // open: en
  Multiplexer multiplexer_25 (
    .in0(multiplexer_9_out), .in1(multiplexer_11_out), .out(multiplexer_25_out), .sel(Shift_Amount[1]));  // open: en
  Multiplexer multiplexer_26 (
    .in0(multiplexer_10_out), .in1(multiplexer_12_out), .out(multiplexer_26_out), .sel(Shift_Amount[1]));  // open: en
  Multiplexer multiplexer_27 (
    .in0(multiplexer_11_out), .in1(multiplexer_13_out), .out(multiplexer_27_out), .sel(Shift_Amount[1]));  // open: en
  Multiplexer multiplexer_28 (
    .in0(multiplexer_12_out), .in1(multiplexer_14_out), .out(multiplexer_28_out), .sel(Shift_Amount[1]));  // open: en
  Multiplexer multiplexer_29 (
    .in0(multiplexer_13_out), .in1(multiplexer_15_out), .out(multiplexer_29_out), .sel(Shift_Amount[1]));  // open: en
  Multiplexer multiplexer_30 (
    .in0(multiplexer_14_out), .in1(multiplexer_16_out), .out(multiplexer_30_out), .sel(Shift_Amount[1]));  // open: en
  Multiplexer multiplexer_31 (
    .in0(multiplexer_15_out), .in1(Being_Shifted[15]), .out(multiplexer_31_out), .sel(Shift_Amount[1]));  // open: en
  Multiplexer multiplexer_32 (
    .in0(multiplexer_16_out), .in1(Being_Shifted[15]), .out(multiplexer_32_out), .sel(Shift_Amount[1]));  // open: en
  Multiplexer multiplexer_33 (
    .in0(multiplexer_17_out), .in1(multiplexer_21_out), .out(multiplexer_33_out), .sel(Shift_Amount[2]));  // open: en
  Multiplexer multiplexer_34 (
    .in0(multiplexer_18_out), .in1(multiplexer_22_out), .out(multiplexer_34_out), .sel(Shift_Amount[2]));  // open: en
  Multiplexer multiplexer_35 (
    .in0(multiplexer_19_out), .in1(multiplexer_23_out), .out(multiplexer_35_out), .sel(Shift_Amount[2]));  // open: en
  Multiplexer multiplexer_36 (
    .in0(multiplexer_20_out), .in1(multiplexer_24_out), .out(multiplexer_36_out), .sel(Shift_Amount[2]));  // open: en
  Multiplexer multiplexer_37 (
    .in0(multiplexer_21_out), .in1(multiplexer_25_out), .out(multiplexer_37_out), .sel(Shift_Amount[2]));  // open: en
  Multiplexer multiplexer_38 (
    .in0(multiplexer_22_out), .in1(multiplexer_26_out), .out(multiplexer_38_out), .sel(Shift_Amount[2]));  // open: en
  Multiplexer multiplexer_39 (
    .in0(multiplexer_23_out), .in1(multiplexer_27_out), .out(multiplexer_39_out), .sel(Shift_Amount[2]));  // open: en
  Multiplexer multiplexer_40 (
    .in0(multiplexer_24_out), .in1(multiplexer_28_out), .out(multiplexer_40_out), .sel(Shift_Amount[2]));  // open: en
  Multiplexer multiplexer_41 (
    .in0(multiplexer_25_out), .in1(multiplexer_29_out), .out(multiplexer_41_out), .sel(Shift_Amount[2]));  // open: en
  Multiplexer multiplexer_42 (
    .in0(multiplexer_26_out), .in1(multiplexer_30_out), .out(multiplexer_42_out), .sel(Shift_Amount[2]));  // open: en
  Multiplexer multiplexer_43 (
    .in0(multiplexer_27_out), .in1(multiplexer_31_out), .out(multiplexer_43_out), .sel(Shift_Amount[2]));  // open: en
  Multiplexer multiplexer_44 (
    .in0(multiplexer_28_out), .in1(multiplexer_32_out), .out(multiplexer_44_out), .sel(Shift_Amount[2]));  // open: en
  Multiplexer multiplexer_45 (
    .in0(multiplexer_29_out), .in1(Being_Shifted[15]), .out(multiplexer_45_out), .sel(Shift_Amount[2]));  // open: en
  Multiplexer multiplexer_46 (
    .in0(multiplexer_30_out), .in1(Being_Shifted[15]), .out(multiplexer_46_out), .sel(Shift_Amount[2]));  // open: en
  Multiplexer multiplexer_47 (
    .in0(multiplexer_31_out), .in1(Being_Shifted[15]), .out(multiplexer_47_out), .sel(Shift_Amount[2]));  // open: en
  Multiplexer multiplexer_48 (
    .in0(multiplexer_32_out), .in1(Being_Shifted[15]), .out(multiplexer_48_out), .sel(Shift_Amount[2]));  // open: en
  Multiplexer multiplexer_49 (
    .in0(multiplexer_33_out), .in1(multiplexer_41_out), .out(out_3[0]), .sel(Shift_Amount[3]));  // open: en
  Multiplexer multiplexer_50 (
    .in0(multiplexer_34_out), .in1(multiplexer_42_out), .out(out_3[1]), .sel(Shift_Amount[3]));  // open: en
  Multiplexer multiplexer_51 (
    .in0(multiplexer_35_out), .in1(multiplexer_43_out), .out(out_3[2]), .sel(Shift_Amount[3]));  // open: en
  Multiplexer multiplexer_52 (
    .in0(multiplexer_36_out), .in1(multiplexer_44_out), .out(out_3[3]), .sel(Shift_Amount[3]));  // open: en
  Multiplexer multiplexer_53 (
    .in0(multiplexer_37_out), .in1(multiplexer_45_out), .out(out_3[4]), .sel(Shift_Amount[3]));  // open: en
  Multiplexer multiplexer_54 (
    .in0(multiplexer_38_out), .in1(multiplexer_46_out), .out(out_3[5]), .sel(Shift_Amount[3]));  // open: en
  Multiplexer multiplexer_55 (
    .in0(multiplexer_39_out), .in1(multiplexer_47_out), .out(out_3[6]), .sel(Shift_Amount[3]));  // open: en
  Multiplexer multiplexer_56 (
    .in0(multiplexer_40_out), .in1(multiplexer_48_out), .out(out_3[7]), .sel(Shift_Amount[3]));  // open: en
  Multiplexer multiplexer_57 (
    .in0(multiplexer_41_out), .in1(Being_Shifted[15]), .out(out_3[8]), .sel(Shift_Amount[3]));  // open: en
  Multiplexer multiplexer_58 (
    .in0(multiplexer_42_out), .in1(Being_Shifted[15]), .out(out_3[9]), .sel(Shift_Amount[3]));  // open: en
  Multiplexer multiplexer_59 (
    .in0(multiplexer_43_out), .in1(Being_Shifted[15]), .out(out_3[10]), .sel(Shift_Amount[3]));  // open: en
  Multiplexer multiplexer_60 (
    .in0(multiplexer_44_out), .in1(Being_Shifted[15]), .out(out_3[11]), .sel(Shift_Amount[3]));  // open: en
  Multiplexer multiplexer_61 (
    .in0(multiplexer_45_out), .in1(Being_Shifted[15]), .out(out_3[12]), .sel(Shift_Amount[3]));  // open: en
  Multiplexer multiplexer_62 (
    .in0(multiplexer_46_out), .in1(Being_Shifted[15]), .out(out_3[13]), .sel(Shift_Amount[3]));  // open: en
  Multiplexer multiplexer_63 (
    .in0(multiplexer_47_out), .in1(Being_Shifted[15]), .out(out_3[14]), .sel(Shift_Amount[3]));  // open: en
  Multiplexer multiplexer_64 (
    .in0(multiplexer_48_out), .in1(Being_Shifted[15]), .out(out_3[15]), .sel(Shift_Amount[3]));  // open: en
endmodule

module Add_Long_Offset (
  input  [15:0] In_Left,
  input  [15:0] In_Right,
  output [15:0] out_3
);

  Adder adder_1 (.in_1({{5{In_Left[11]}}, In_Left[10:0]}), .in_2(In_Right), .out_3(out_3));
endmodule

module Step_State (
  input  Timeout,
  input  CC_N,
  input  CC_Z,
  input  PSW_P,
  input  Clear,
  input  Enable,
  input  [3:0] Opcode_In,
  input  Clock_In,
  output [3:0] out_9,
  output Fetch,
  output Execute,
  output Trap,
  output B0_Out
);

  wire and_1_out, and_2_out, and_3_out, and_4_out, and_5_out, and_6_out, and_7_out, and_8_out, and_9_out,
       and_10_out, and_11_out, and_12_out, and_13_out, and_14_out, and_15_out, Data_A0_qn, Data_B0_qn,
       Data_C0_qn, Data_D0_qn, decoder_1_out6, decoder_1_out7, decoder_1_out8, decoder_1_out9,
       decoder_1_out10, decoder_1_out11, decoder_1_out12, decoder_1_out13, decoder_1_out14, decoder_1_out15,
       not_1_out, not_2_out, not_3_out, not_4_out, not_5_out, not_6_out, or_1_out, or_2_out, or_3_out,
       or_4_out, or_5_out, or_6_out, or_7_out, zb_1_zb, zc_1_zb, zd_1_zd;

  Decoder #(.select(4)) decoder_1 (
    .out6(decoder_1_out6), .out7(decoder_1_out7), .out8(decoder_1_out8), .out9(decoder_1_out9),
    .out10(decoder_1_out10), .out11(decoder_1_out11), .out12(decoder_1_out12), .out13(decoder_1_out13),
    .out14(decoder_1_out14), .out15(decoder_1_out15), .sel(Opcode_In), .en(1'b1));  // open: out0, out1, out2, out3, out4, out5
  and and_1 (and_1_out, decoder_1_out9, CC_N);
  or or_1 (or_1_out, and_1_out, and_2_out, decoder_1_out11);
  and and_2 (and_2_out, decoder_1_out10, CC_Z);
  and and_3 (and_3_out, or_2_out, PSW_P);
  or or_2 (or_2_out, decoder_1_out14, decoder_1_out15);
  and and_4 (and_4_out, or_2_out, not_1_out);
  and and_5 (and_5_out, decoder_1_out9, not_3_out);
  not not_1 (not_1_out, PSW_P);
  or or_3 (or_3_out, and_5_out, and_6_out);
  and and_6 (and_6_out, decoder_1_out10, not_2_out);
  not not_2 (not_2_out, CC_Z);
  not not_3 (not_3_out, CC_N);
  ZB zb_1 (
    .A(or_1_out), .D(and_4_out), .E(or_3_out), .Timeout(Timeout), .Opcode_6(decoder_1_out6),
    .Opcode_7(decoder_1_out7), .Opcode_8(decoder_1_out8), .ZB(zb_1_zb));
  ZC zc_1 (
    .C(and_3_out), .D(and_4_out), .E(or_3_out), .Timeout(Timeout), .Opcode_6(decoder_1_out6),
    .Opcode_7(decoder_1_out7), .Opcode_8(decoder_1_out8), .Opcode_13(decoder_1_out13), .ZB(zc_1_zb));
  ZD zd_1 (
    .A(or_1_out), .C(and_3_out), .Opcode_6(decoder_1_out6), .Opcode_7(decoder_1_out7),
    .Opcode_12(decoder_1_out12), .ZD(zd_1_zd));
  not not_4 (not_4_out, or_3_out);
  not not_5 (not_5_out, and_4_out);
  and and_7 (and_7_out, Data_A0_qn, Data_C0_qn, zb_1_zb);
  and and_8 (and_8_out, Data_A0_qn, B0_Out, out_9[1], Data_D0_qn);
  and and_9 (and_9_out, Execute, not_6_out, Timeout);
  not not_6 (not_6_out, and_10_out);
  and and_10 (and_10_out, Execute, Data_B0_qn, decoder_1_out6, out_9[1], out_9[0]);
  and and_11 (and_11_out, Data_A0_qn, Data_C0_qn, zc_1_zb);
  and and_12 (and_12_out, Data_A0_qn, out_9[1], Data_D0_qn);
  and and_13 (and_13_out, zd_1_zd, Data_A0_qn, Data_C0_qn);
  and and_14 (and_14_out, Data_A0_qn, out_9[1], Data_D0_qn);
  and and_15 (and_15_out, not_4_out, Data_A0_qn, Data_C0_qn, not_5_out);
  or or_4 (or_4_out, and_10_out, and_15_out);
  or or_5 (or_5_out, and_7_out, and_8_out, and_9_out);
  or or_6 (or_6_out, and_9_out, and_11_out, and_12_out);
  or or_7 (or_7_out, and_13_out, and_14_out);
  D_Flip_Flop Data_A0 (
    .clk(Clock_In), .D(or_4_out), .Q(Execute), .Qn(Data_A0_qn), .preset(1'b0), .en(Enable), .reset(Clear));
  D_Flip_Flop Data_B0 (
    .clk(Clock_In), .D(or_5_out), .Q(B0_Out), .Qn(Data_B0_qn), .preset(1'b0), .en(Enable), .reset(Clear));
  D_Flip_Flop Data_C0 (
    .clk(Clock_In), .D(or_6_out), .Q(out_9[1]), .Qn(Data_C0_qn), .preset(1'b0), .en(Enable), .reset(Clear));
  D_Flip_Flop Data_D0 (
    .clk(Clock_In), .D(or_7_out), .Q(out_9[0]), .Qn(Data_D0_qn), .preset(1'b0), .en(Enable), .reset(Clear));
  and and_16 (Fetch, Data_A0_qn, Data_C0_qn);
  and and_17 (Trap, Data_A0_qn, out_9[1]);

  assign out_9[3:2] = {Execute, B0_Out};

  // Notes on the sheet:
  //   A
  //   B
  //   C
  //   D
  //   E
endmodule

module ZB (
  input  A,
  input  D,
  input  E,
  input  Timeout,
  input  Opcode_6,
  input  Opcode_7,
  input  Opcode_8,
  output ZB
);

  wire and_1_out, not_1_out, or_1_out;

  not not_1 (not_1_out, Timeout);
  and and_1 (and_1_out, E, not_1_out);
  or or_1 (or_1_out, A, D, and_1_out, Opcode_6, Opcode_7, Opcode_8);
  not not_2 (ZB, or_1_out);
endmodule

module ZC (
  input  C,
  input  D,
  input  E,
  input  Timeout,
  input  Opcode_6,
  input  Opcode_7,
  input  Opcode_8,
  input  Opcode_13,
  output ZB
);

  wire and_1_out;

  and and_1 (and_1_out, E, Timeout);
  or or_1 (ZB, C, D, Opcode_6, and_1_out, Opcode_7, Opcode_8, Opcode_13);
endmodule

module ZD (
  input  A,
  input  C,
  input  Opcode_6,
  input  Opcode_7,
  input  Opcode_12,
  output ZD
);

  or or_1 (ZD, A, C, Opcode_6, Opcode_7, Opcode_12);
endmodule

module _4_Bit_Adder (
  input  [3:0] in_1,
  input  [3:0] in_2,
  input  C_In,
  output C_Out,
  output [3:0] out_5
);

  wire and_1_out, and_2_out, and_3_out, and_4_out, lookahead_generator_1_out_11,
       lookahead_generator_1_out_12, lookahead_generator_1_out_13, xor_1_out, xor_2_out, xor_3_out, xor_4_out;

  and and_1 (and_1_out, in_1[3], in_2[3]);
  and and_2 (and_2_out, in_1[1], in_2[1]);
  and and_3 (and_3_out, in_1[0], in_2[0]);
  xor xor_1 (xor_1_out, in_1[3], in_2[3]);
  xor xor_2 (xor_2_out, in_1[2], in_2[2]);
  and and_4 (and_4_out, in_1[2], in_2[2]);
  xor xor_3 (xor_3_out, in_1[1], in_2[1]);
  xor xor_4 (xor_4_out, in_1[0], in_2[0]);
  Lookahead_Generator lookahead_generator_1 (
    .P3(xor_1_out), .G3(and_1_out), .P2(xor_2_out), .G2(and_4_out), .P1(xor_3_out), .G1(and_2_out),
    .P0(xor_4_out), .G0(and_3_out), .C_In(C_In), .out_10(C_Out), .out_11(lookahead_generator_1_out_11),
    .out_12(lookahead_generator_1_out_12), .out_13(lookahead_generator_1_out_13));
  xor xor_5 (out_5[3], lookahead_generator_1_out_11, xor_1_out);
  xor xor_6 (out_5[2], lookahead_generator_1_out_12, xor_2_out);
  xor xor_7 (out_5[1], lookahead_generator_1_out_13, xor_3_out);
  xor xor_8 (out_5[0], xor_4_out, C_In);
endmodule

module Lookahead_Generator (
  input  P3,
  input  G3,
  input  P2,
  input  G2,
  input  P1,
  input  G1,
  input  P0,
  input  G0,
  input  C_In,
  output out_10,
  output out_11,
  output out_12,
  output out_13
);

  wire and_1_out, and_2_out, and_3_out, and_4_out, and_5_out, and_6_out, and_7_out, and_8_out, and_9_out,
       and_10_out;

  and and_1 (and_1_out, P3, P2, P1, P0, C_In);
  and and_2 (and_2_out, P3, P2, P1, G1);
  and and_3 (and_3_out, P3, P2, G2);
  and and_4 (and_4_out, P3, G3);
  and and_5 (and_5_out, C_In, P0, P1, P2);
  and and_6 (and_6_out, P1, G1, P2);
  and and_7 (and_7_out, P2, G1);
  and and_8 (and_8_out, P0, C_In, P1);
  and and_9 (and_9_out, P1, G0);
  and and_10 (and_10_out, P0, C_In);
  or or_1 (out_10, and_1_out, and_2_out, and_3_out, and_4_out, G3);
  or or_2 (out_11, and_5_out, and_6_out, and_7_out, G2);
  or or_3 (out_12, and_8_out, and_9_out, G1);
  or or_4 (out_13, and_10_out, G0);
endmodule

module _16_Bit_Adder (
  input  [15:0] in_1,
  input  [15:0] in_2,
  output [15:0] out_3
);

  wire n4_bit_adder_2_c_out, n4_bit_adder_3_c_out, n4_bit_adder_4_c_out;

  _4_Bit_Adder u_4_bit_adder_1 (
    .in_1(in_1[3:0]), .in_2(in_2[3:0]), .C_In(n4_bit_adder_2_c_out), .out_5(out_3[3:0]));  // open: C_Out
  _4_Bit_Adder u_4_bit_adder_2 (
    .in_1(in_1[7:4]), .in_2(in_2[7:4]), .C_In(n4_bit_adder_3_c_out), .C_Out(n4_bit_adder_2_c_out),
    .out_5(out_3[7:4]));
  _4_Bit_Adder u_4_bit_adder_3 (
    .in_1(in_1[11:8]), .in_2(in_2[11:8]), .C_In(n4_bit_adder_4_c_out), .C_Out(n4_bit_adder_3_c_out),
    .out_5(out_3[11:8]));
  _4_Bit_Adder u_4_bit_adder_4 (
    .in_1(in_1[15:12]), .in_2(in_2[15:12]), .C_In(1'b0), .C_Out(n4_bit_adder_4_c_out), .out_5(out_3[15:12]));
endmodule
